// Logisim project tmi.circ as structural Verilog: 7 circuits, main circuit cell
module main (
);

  wire cell_1_clk_2, cell_1_is_active_2, cell_1_set_head, cell_2_clk_2, cell_2_is_active, cell_2_is_active_2,
       cell_2_set_head, cell_2_set_tail, cell_3_clk_2, cell_3_is_active, cell_3_is_active_2, cell_3_set_head,
       cell_3_set_tail, cell_4_clk_2, cell_4_is_active, cell_4_is_active_2, cell_4_set_head, cell_4_set_tail,
       cell_5_is_active, cell_5_set_tail, clock_1_out, cpu_1_cell_clk, cpu_1_fake_act, cpu_1_is_inited,
       cpu_1_is_on, cpu_1_kbd_clk, cpu_1_tape_next, cpu_1_tape_prev, cpu_1_tape_rst, cpu_1_tty_clk,
       cpu_1_wait_kbd, keyboard_1_avail, START_out;
  wire [2:0] cell_1_cmd_2, cell_1_dbg_led, cell_2_cmd_2, cell_2_dbg_led, cell_3_cmd_2, cell_3_dbg_led,
       cell_4_cmd_2, cell_4_dbg_led, cell_5_cmd_2, cell_5_dbg_led, cpu_1_cmd;
  wire [3:0] cell_1_dbg_mem, cell_1_dbg_mem_2, cell_2_dbg_mem, cell_2_dbg_mem_2, cell_3_dbg_mem,
       cell_3_dbg_mem_2, cell_4_dbg_mem, cell_4_dbg_mem_2, rom_1_data, tape_1_bf_cmd;
  wire [6:0] cpu_1_disp, keyboard_1_data;
  wire [7:0] cell_1_data_in_2, cell_1_data_out_2, cell_2_data_in_2, cell_2_data_out_2, cell_3_data_in_2,
       cell_3_data_out_2, cell_4_data_in_2, cell_4_data_out_2, cell_5_data_in_2, cell_5_data_out_2,
       cell_5_dbg_mem, cpu_1_data_to_cell;
  wire [11:0] tape_1_address;

  LED NEED_INPUT (.in(cpu_1_wait_kbd));
  tape tape_1 (
    .ADDRESS(tape_1_address), .DATA(rom_1_data), .BF_CMD(tape_1_bf_cmd), .BF_NEXT(cpu_1_tape_next),
    .BF_PREV(cpu_1_tape_prev), .TAPE_RST(cpu_1_tape_rst));
  Clock clock_1 (.out(clock_1_out));
  Button START (.out(START_out));
  Keyboard keyboard_1 (.clk(cpu_1_kbd_clk), .avail(keyboard_1_avail), .data(keyboard_1_data));  // open: re, clr
  ROM #(.addrWidth(12), .dataWidth(4)) rom_1 (.addr(tape_1_address), .data(rom_1_data));  // open: sel
  ROM #(.addrWidth(12), .dataWidth(4)) rom_2 ();  // open: addr, data, sel
  LED IS_ON (.in(cpu_1_is_on));
  LED IS_INITED (.in(cpu_1_is_inited));
  cpu cpu_1 (
    .CUR_BF(tape_1_bf_cmd), .TAPE_NEXT(cpu_1_tape_next), .TAPE_PREV(cpu_1_tape_prev),
    .TAPE_RST(cpu_1_tape_rst), .IS_INITED(cpu_1_is_inited), .IS_ON(cpu_1_is_on), .DISP(cpu_1_disp),
    .TTY_CLK(cpu_1_tty_clk), .CLK(clock_1_out), .TURN_ON(START_out), .WAIT_KBD(cpu_1_wait_kbd),
    .KBD_CLK(cpu_1_kbd_clk), .CHAR(keyboard_1_data), .HAS_CHAR(keyboard_1_avail), .FAKE_ACT(cpu_1_fake_act),
    .DATA_TO_CELL(cpu_1_data_to_cell), .DATA_FROM_CELL(cell_1_data_out_2), .CMD(cpu_1_cmd),
    .CELL_CLK(cpu_1_cell_clk));
  LED HAS_INPUT (.in(keyboard_1_avail));
  TTY #(.rows(20), .cols(80)) tty_1 (.data(cpu_1_disp), .clk(cpu_1_tty_clk));  // open: we, clr
  \cell  cell_1 (
    .IS_ACTIVE_LEFT(cpu_1_fake_act), .DATA_IN(cpu_1_data_to_cell), .DATA_OUT_2(cell_1_data_out_2),
    .CMD(cpu_1_cmd), .CLK(cpu_1_cell_clk), .IS_TAIL(cell_2_set_tail), .SET_HEAD(cell_1_set_head),
    .IS_ACTIVE_RIGHT(cell_2_is_active), .IS_ACTIVE_2(cell_1_is_active_2), .DATA_IN_2(cell_1_data_in_2),
    .DATA_OUT(cell_2_data_out_2), .CMD_2(cell_1_cmd_2), .CLK_2(cell_1_clk_2),
    .DBG_MEM({cell_1_dbg_mem_2, cell_1_dbg_mem}), .DBG_LED(cell_1_dbg_led));  // open: SET_TAIL, IS_HEAD, IS_ACTIVE
  DotMatrix #(.matrixcols(3), .matrixrows(1)) dotmatrix_1 (
    .col0(cell_1_dbg_led[0]), .col1(cell_1_dbg_led[1]), .col2(cell_1_dbg_led[2]));
  Hex_Digit_Display hex_digit_display_1 (.value(cell_1_dbg_mem));  // open: dp
  Hex_Digit_Display hex_digit_display_2 (.value(cell_1_dbg_mem_2));  // open: dp
  Hex_Digit_Display hex_digit_display_3 (.value({1'b0, keyboard_1_data[6:4]}));  // open: dp
  Hex_Digit_Display hex_digit_display_4 (.value(keyboard_1_data[3:0]));  // open: dp
  Hex_Digit_Display hex_digit_display_5 (.value(cell_2_dbg_mem_2));  // open: dp
  \cell  cell_2 (
    .SET_TAIL(cell_2_set_tail), .IS_HEAD(cell_1_set_head), .IS_ACTIVE(cell_2_is_active),
    .IS_ACTIVE_LEFT(cell_1_is_active_2), .DATA_IN(cell_1_data_in_2), .DATA_OUT_2(cell_2_data_out_2),
    .CMD(cell_1_cmd_2), .CLK(cell_1_clk_2), .IS_TAIL(cell_3_set_tail), .SET_HEAD(cell_2_set_head),
    .IS_ACTIVE_RIGHT(cell_3_is_active), .IS_ACTIVE_2(cell_2_is_active_2), .DATA_IN_2(cell_2_data_in_2),
    .DATA_OUT(cell_3_data_out_2), .CMD_2(cell_2_cmd_2), .CLK_2(cell_2_clk_2),
    .DBG_MEM({cell_2_dbg_mem_2, cell_2_dbg_mem}), .DBG_LED(cell_2_dbg_led));
  DotMatrix #(.matrixcols(3), .matrixrows(1)) dotmatrix_2 (
    .col0(cell_2_dbg_led[0]), .col1(cell_2_dbg_led[1]), .col2(cell_2_dbg_led[2]));
  Hex_Digit_Display hex_digit_display_6 (.value(cell_2_dbg_mem));  // open: dp
  \cell  cell_3 (
    .SET_TAIL(cell_3_set_tail), .IS_HEAD(cell_2_set_head), .IS_ACTIVE(cell_3_is_active),
    .IS_ACTIVE_LEFT(cell_2_is_active_2), .DATA_IN(cell_2_data_in_2), .DATA_OUT_2(cell_3_data_out_2),
    .CMD(cell_2_cmd_2), .CLK(cell_2_clk_2), .IS_TAIL(cell_4_set_tail), .SET_HEAD(cell_3_set_head),
    .IS_ACTIVE_RIGHT(cell_4_is_active), .IS_ACTIVE_2(cell_3_is_active_2), .DATA_IN_2(cell_3_data_in_2),
    .DATA_OUT(cell_4_data_out_2), .CMD_2(cell_3_cmd_2), .CLK_2(cell_3_clk_2),
    .DBG_MEM({cell_3_dbg_mem_2, cell_3_dbg_mem}), .DBG_LED(cell_3_dbg_led));
  DotMatrix #(.matrixcols(3), .matrixrows(1)) dotmatrix_3 (
    .col0(cell_3_dbg_led[0]), .col1(cell_3_dbg_led[1]), .col2(cell_3_dbg_led[2]));
  Hex_Digit_Display hex_digit_display_7 (.value(cell_3_dbg_mem_2));  // open: dp
  Hex_Digit_Display hex_digit_display_8 (.value(cell_3_dbg_mem));  // open: dp
  Hex_Digit_Display hex_digit_display_9 (.value(cell_4_dbg_mem_2));  // open: dp
  \cell  cell_4 (
    .SET_TAIL(cell_4_set_tail), .IS_HEAD(cell_3_set_head), .IS_ACTIVE(cell_4_is_active),
    .IS_ACTIVE_LEFT(cell_3_is_active_2), .DATA_IN(cell_3_data_in_2), .DATA_OUT_2(cell_4_data_out_2),
    .CMD(cell_3_cmd_2), .CLK(cell_3_clk_2), .IS_TAIL(cell_5_set_tail), .SET_HEAD(cell_4_set_head),
    .IS_ACTIVE_RIGHT(cell_5_is_active), .IS_ACTIVE_2(cell_4_is_active_2), .DATA_IN_2(cell_4_data_in_2),
    .DATA_OUT(cell_5_data_out_2), .CMD_2(cell_4_cmd_2), .CLK_2(cell_4_clk_2),
    .DBG_MEM({cell_4_dbg_mem_2, cell_4_dbg_mem}), .DBG_LED(cell_4_dbg_led));
  DotMatrix #(.matrixcols(3), .matrixrows(1)) dotmatrix_4 (
    .col0(cell_4_dbg_led[0]), .col1(cell_4_dbg_led[1]), .col2(cell_4_dbg_led[2]));
  Hex_Digit_Display hex_digit_display_10 (.value(cell_4_dbg_mem));  // open: dp
  \cell  cell_5 (
    .SET_TAIL(cell_5_set_tail), .IS_HEAD(cell_4_set_head), .IS_ACTIVE(cell_5_is_active),
    .IS_ACTIVE_LEFT(cell_4_is_active_2), .DATA_IN(cell_4_data_in_2), .DATA_OUT_2(cell_5_data_out_2),
    .CMD(cell_4_cmd_2), .CLK(cell_4_clk_2), .DATA_IN_2(cell_5_data_in_2), .CMD_2(cell_5_cmd_2),
    .DBG_MEM(cell_5_dbg_mem), .DBG_LED(cell_5_dbg_led));  // open: IS_TAIL, SET_HEAD, IS_ACTIVE_RIGHT, IS_ACTIVE_2, DATA_OUT, CLK_2
  DotMatrix #(.matrixcols(3), .matrixrows(1)) dotmatrix_5 (
    .col0(cell_5_dbg_led[0]), .col1(cell_5_dbg_led[1]), .col2(cell_5_dbg_led[2]));
  Hex_Digit_Display hex_digit_display_11 (.value(cell_5_dbg_mem[7:4]));  // open: dp
  Hex_Digit_Display hex_digit_display_12 (.value(cell_5_dbg_mem[3:0]));  // open: dp
  Hex_Digit_Display hex_digit_display_13 (.value(cell_5_data_in_2[3:0]));  // open: dp
  Hex_Digit_Display hex_digit_display_14 (.value(cell_5_data_in_2[7:4]));  // open: dp
  Hex_Digit_Display hex_digit_display_15 (.value({1'b0, cell_5_cmd_2}));  // open: dp

  // Notes on the sheet:
  //   [Hello, world]
  //   Hello, world
  //   contents of rom_1 (hex, n*v repeats v):
  //   10*6 1 3 7*6 3 10*6 3 6 6 6 3 6 4*2 7 0 3 6 6 4 3 6 4 7*6 4 4 6 6 6 4 3 6 6 4 2 2 15*6 4 3 4 6 6 6 4
  //   6*7 4 8*7 4 3 6 4 3 4 8
  //   contents of rom_2 (hex, n*v repeats v):
  //   72*6 4 29*6 4 7*6 4 4 6 6 6 4 79*7 4 55*6 4 24*6 4 6 6 6 4 6*7 4 8*7 4 67*7 4 23*7 4 8
endmodule

// memcell
module \cell  (
  input  IS_TAIL,
  input  IS_HEAD,
  input  IS_ACTIVE_RIGHT,
  input  IS_ACTIVE_LEFT,
  input  [7:0] DATA_IN,
  input  [7:0] DATA_OUT,
  input  [2:0] CMD,
  input  CLK,
  output SET_TAIL,
  output SET_HEAD,
  output IS_ACTIVE,
  output IS_ACTIVE_2,
  output [7:0] DATA_IN_2,
  output [7:0] DATA_OUT_2,
  output [2:0] CMD_2,
  output CLK_2,
  output [7:0] DBG_MEM,
  output [2:0] DBG_LED
);

  wire and_1_out, and_2_out, and_6_out, ARITH, bitselector_1_out, bitselector_2_out, COUNT, decoder_1_out0,
       LOAD, minus_ACT, not_1_out, not_2_out, not_3_out, not_4_out, not_5_out, plus_ACT, RST, RW, s_r_ff_1_q,
       SHIFT, WRITE;
  wire [7:0] controlled_buffer_5_out;

  Decoder #(.select(2), .disabled(0), .enable("false")) decoder_1 (
    .out0(decoder_1_out0), .out1(SHIFT), .out2(RW), .out3(ARITH), .sel(CMD[2:1]));
  and and_1 (and_1_out, CMD[0], decoder_1_out0);
  BitSelector #(.width(2)) bitselector_1 (.in({IS_TAIL, IS_HEAD}), .out(bitselector_1_out), .sel(CMD[0]));
  not not_1 (not_1_out, bitselector_1_out);
  not not_2 (not_2_out, DBG_LED[1]);
  BitSelector #(.width(2)) bitselector_2 (
    .in({IS_ACTIVE_LEFT, IS_ACTIVE_RIGHT}), .out(bitselector_2_out), .sel(CMD[0]));
  and and_2 (and_2_out, ARITH, DBG_LED[1]);
  and and_3 (WRITE, RW, CMD[0], DBG_LED[1]);
  Pull_Resistor #(.pull(1)) pull_resistor_1 (.node(IS_HEAD));
  Pull_Resistor pull_resistor_2 (.node(IS_ACTIVE_LEFT));
  D_Flip_Flop d_ff_1 (.clk(CLK), .D(and_1_out), .Q(RST), .reset(not_3_out));  // open: Qn, preset, en
  not not_3 (not_3_out, and_1_out);
  assign LOAD = and_2_out ? CMD[0] : 1'bz;  // Controlled_Buffer controlled_buffer_1
  assign COUNT = and_2_out ? 1'b1 : 1'bz;  // Controlled_Buffer controlled_buffer_2
  assign LOAD = WRITE ? 1'b1 : 1'bz;  // Controlled_Buffer controlled_buffer_3
  assign COUNT = WRITE ? 1'b0 : 1'bz;  // Controlled_Buffer controlled_buffer_4
  Pull_Resistor pull_resistor_3 (.node(DATA_IN));
  Pull_Resistor pull_resistor_4 (.node(CMD));
  Pull_Resistor pull_resistor_5 (.node(CLK));
  and and_4 (minus_ACT, DBG_LED[1], SHIFT, not_1_out);
  and and_5 (plus_ACT, not_2_out, SHIFT, bitselector_2_out);
  assign controlled_buffer_5_out = WRITE ? DATA_IN : 8'bz;  // Controlled_Buffer controlled_buffer_5
  Pull_Resistor #(.pull(1)) pull_resistor_6 (.node(IS_TAIL));
  Pull_Resistor pull_resistor_7 (.node(IS_ACTIVE_RIGHT));
  S_R_Flip_Flop s_r_ff_1 (.S(plus_ACT), .clk(CLK), .R(minus_ACT), .Q(s_r_ff_1_q), .reset(RST));  // open: Qn, preset, en
  Pull_Resistor pull_resistor_8 (.node(LOAD));
  Counter counter_1 (
    .load(LOAD), .D(controlled_buffer_5_out), .count(COUNT), .Q(DBG_MEM), .clk(CLK), .clr(RST));  // open: carry
  Pull_Resistor pull_resistor_9 (.node(COUNT));
  D_Flip_Flop d_ff_2 (.clk(not_4_out), .D(s_r_ff_1_q), .Q(DBG_LED[1]), .reset(RST));  // open: Qn, preset, en
  not not_4 (not_4_out, CLK);
  assign DATA_OUT = and_6_out ? DBG_MEM : 8'bz;  // Controlled_Buffer controlled_buffer_6
  and and_6 (and_6_out, not_5_out, DBG_LED[1], RW);
  not not_5 (not_5_out, CMD[0]);

  assign CLK_2 = CLK;
  assign CMD_2 = CMD;
  assign DATA_IN_2 = DATA_IN;
  assign DATA_OUT_2 = DATA_OUT;
  assign {DBG_LED[2], DBG_LED[0]} = {IS_TAIL, IS_HEAD};
  assign IS_ACTIVE = DBG_LED[1];
  assign IS_ACTIVE_2 = DBG_LED[1];
  assign SET_HEAD = 1'b0;
  assign SET_TAIL = 1'b0;

  // Other names for the same wires on the sheet: AR = IS_ACTIVE_RIGHT; AL = IS_ACTIVE_LEFT; HEAD = IS_HEAD;
  //   ACT = DBG_LED[1]; TAIL = IS_TAIL; IN[7:0] = DATA_IN; OUT[7:0] = DATA_OUT
endmodule

module tape (
  input  [3:0] DATA,
  input  BF_NEXT,
  input  BF_PREV,
  input  TAPE_RST,
  output [11:0] ADDRESS,
  output [3:0] BF_CMD
);

  wire or_1_out;

  or or_1 (or_1_out, BF_PREV, BF_NEXT);
  Pull_Resistor pull_resistor_1 (.node(BF_NEXT));
  Pull_Resistor pull_resistor_2 (.node(BF_PREV));
  Counter #(.width(12), .max('hfff)) counter_1 (
    .load(BF_PREV), .count(or_1_out), .Q(ADDRESS), .clk(or_1_out), .clr(TAPE_RST));  // open: D, carry

  assign BF_CMD = DATA;

  // Other names for the same wires on the sheet: ADDR[11:0] = ADDRESS; NEXT = BF_NEXT; PREV = BF_PREV
endmodule

module cpu (
  input  [3:0] CUR_BF,
  input  [7:0] DATA_FROM_CELL,
  input  CLK,
  input  TURN_ON,
  input  [6:0] CHAR,
  input  HAS_CHAR,
  output IS_INITED,
  output IS_ON,
  output [6:0] DISP,
  output TTY_CLK,
  output FAKE_ACT,
  output [7:0] DATA_TO_CELL,
  output TAPE_NEXT,
  output TAPE_PREV,
  output [2:0] CMD,
  output TAPE_RST,
  output CELL_CLK,
  output WAIT_KBD,
  output KBD_CLK
);

  wire and_1_out, and_2_out, and_3_out, and_4_out, and_5_out, and_6_out, and_7_out, and_8_out, and_9_out,
       and_10_out, and_11_out, and_12_out, and_13_out, and_14_out, and_15_out, and_16_out, and_18_out,
       and_20_out, and_21_out, CELL_ZERO, CLEAR_ACT, comparator_2_eq, IS_EXEC, IS_EXECR, IS_EXECW0,
       IS_EXECW1, IS_IN_CMD, IS_INIT0, IS_INIT2, IS_INIT3, IS_INIT4, IS_JMP, IS_JMP_CMD, IS_LIKE_JMP_CMD,
       IS_NEXT, IS_OUT_CMD, IS_RDY, IS_SHOW, IS_SIMPLE_CMD, IS_SKIP, IS_STOP, IS_STOP_CMD, IS_WHCHK,
       IS_WHGET, IS_WHILE_CMD, not_1_out, not_2_out, not_3_out, not_4_out, not_5_out, not_6_out, not_7_out,
       not_8_out, or_1_out, or_2_out, STOP_SKIP;
  wire [2:0] NEXT_CMD;
  wire [3:0] CUR_STATE;
  wire [4:0] NEXT_STATE;
  wire [7:0] counter_1_q, NEXT_TO_CELL;
  wire [7:7] DISP_t;

  not not_1 (not_1_out, CLK);
  not not_2 (not_2_out, CLK);
  or or_1 (or_1_out, IS_JMP, IS_SKIP);
  not not_3 (not_3_out, IS_INITED);
  Register #(.width(5)) STATE (.D(NEXT_STATE), .Q({IS_INITED, CUR_STATE}), .clk(not_1_out));  // open: en, clr
  Register CELL_DATA (.D(NEXT_TO_CELL), .Q(DATA_TO_CELL), .clk(not_2_out));  // open: en, clr
  and and_1 (and_1_out, IS_INIT0, IS_ON);
  assign NEXT_STATE = and_1_out ? 5'b00001 : 5'bz;  // Controlled_Buffer controlled_buffer_1
  assign NEXT_STATE = IS_INIT3 ? 5'b00100 : 5'bz;  // Controlled_Buffer controlled_buffer_2
  assign NEXT_CMD = IS_INIT3 ? 3'b011 : 3'bz;  // Controlled_Buffer controlled_buffer_3
  assign NEXT_STATE = IS_SHOW ? 5'b10010 : 5'bz;  // Controlled_Buffer controlled_buffer_4
  assign TTY_CLK = IS_SHOW ? CLK : 1'bz;  // Controlled_Buffer controlled_buffer_5
  assign {DISP_t[7], DISP} = IS_SHOW ? DATA_FROM_CELL : 8'bz;  // Controlled_Buffer controlled_buffer_6
  and and_2 (and_2_out, HAS_CHAR, IS_EXECW0);
  assign NEXT_STATE = and_2_out ? 5'b10101 : 5'bz;  // Controlled_Buffer controlled_buffer_7
  and and_3 (and_3_out, HAS_CHAR, IS_EXECW0);
  assign NEXT_TO_CELL = and_3_out ? {1'b0, CHAR} : 8'bz;  // Controlled_Buffer controlled_buffer_8
  buf buffer_1 (WAIT_KBD, IS_EXECW0);
  not not_4 (not_4_out, CELL_ZERO);
  and and_4 (and_4_out, or_1_out, CLK);
  Decoder #(.select(3), .disabled(0)) decoder_1 (
    .out0(IS_INIT0), .out1(TAPE_RST), .out2(IS_INIT2), .out3(IS_INIT3), .out4(IS_INIT4), .out5(CLEAR_ACT),
    .sel(CUR_STATE[2:0]), .en(not_3_out));  // open: out6, out7
  Decoder #(.select(4), .disabled(0)) decoder_2 (
    .out0(IS_RDY), .out1(IS_EXEC), .out2(IS_NEXT), .out3(IS_EXECR), .out4(IS_EXECW0), .out5(IS_EXECW1),
    .out6(IS_SHOW), .out7(IS_JMP), .out8(IS_SKIP), .out9(IS_WHGET), .out10(IS_WHCHK), .sel(CUR_STATE),
    .en(IS_INITED));  // open: out11, out12, out13, out14, out15
  Pull_Resistor pull_resistor_1 (.node(CLK));
  Hex_Digit_Display hex_digit_display_1 (.value(DATA_TO_CELL[7:4]));  // open: dp
  and and_5 (and_5_out, IS_SIMPLE_CMD, IS_RDY);
  assign NEXT_STATE = and_5_out ? 5'b10001 : 5'bz;  // Controlled_Buffer controlled_buffer_9
  and and_6 (and_6_out, IS_OUT_CMD, IS_RDY);
  assign NEXT_STATE = and_6_out ? 5'b10011 : 5'bz;  // Controlled_Buffer controlled_buffer_10
  and and_7 (and_7_out, IS_WHILE_CMD, IS_RDY);
  assign NEXT_STATE = and_7_out ? 5'b11001 : 5'bz;  // Controlled_Buffer controlled_buffer_11
  and and_8 (and_8_out, IS_WHILE_CMD, IS_RDY);
  assign NEXT_CMD = and_8_out ? 3'b100 : 3'bz;  // Controlled_Buffer controlled_buffer_12
  and and_9 (and_9_out, IS_WHCHK, CELL_ZERO);
  assign NEXT_STATE = and_9_out ? 5'b11000 : 5'bz;  // Controlled_Buffer controlled_buffer_13
  and and_10 (and_10_out, IS_WHCHK, not_4_out);
  assign NEXT_STATE = and_10_out ? 5'b10010 : 5'bz;  // Controlled_Buffer controlled_buffer_14
  and and_11 (and_11_out, IS_JMP_CMD, and_4_out);
  and and_12 (and_12_out, and_4_out, IS_WHILE_CMD);
  Hex_Digit_Display hex_digit_display_2 (.value(DATA_TO_CELL[3:0]));  // open: dp
  Counter counter_1 (.load(and_11_out), .count(or_2_out), .Q(counter_1_q), .clk(or_2_out));  // open: D, carry, clr
  or or_2 (or_2_out, and_11_out, and_12_out);
  assign NEXT_STATE = IS_EXEC ? 5'b10010 : 5'bz;  // Controlled_Buffer controlled_buffer_15
  assign CELL_CLK = IS_EXEC ? CLK : 1'bz;  // Controlled_Buffer controlled_buffer_16
  Comparator #(.mode("unsigned")) comparator_1 (.a(counter_1_q), .b({8{1'b0}}), .eq(STOP_SKIP));  // open: gt, lt
  D_Flip_Flop d_ff_1 (.Q(FAKE_ACT), .preset(TAPE_RST), .reset(CLEAR_ACT));  // open: clk, D, Qn, en
  assign NEXT_STATE = TAPE_RST ? 5'b00010 : 5'bz;  // Controlled_Buffer controlled_buffer_17
  assign NEXT_CMD = TAPE_RST ? 3'b001 : 3'bz;  // Controlled_Buffer controlled_buffer_18
  assign NEXT_STATE = IS_INIT4 ? 5'b00101 : 5'bz;  // Controlled_Buffer controlled_buffer_19
  assign CELL_CLK = IS_INIT4 ? CLK : 1'bz;  // Controlled_Buffer controlled_buffer_20
  not not_5 (not_5_out, HAS_CHAR);
  assign NEXT_STATE = IS_EXECW1 ? 5'b10010 : 5'bz;  // Controlled_Buffer controlled_buffer_21
  assign CELL_CLK = IS_EXECW1 ? CLK : 1'bz;  // Controlled_Buffer controlled_buffer_22
  assign KBD_CLK = IS_EXECW1 ? CLK : 1'bz;  // Controlled_Buffer controlled_buffer_23
  Register #(.width(3)) CELL_CMD (.D(NEXT_CMD), .Q(CMD), .clk(not_6_out));  // open: en, clr
  not not_6 (not_6_out, CLK);
  and and_13 (and_13_out, IS_IN_CMD, not_5_out, IS_RDY);
  and and_14 (and_14_out, IS_IN_CMD, HAS_CHAR, IS_RDY);
  and and_15 (and_15_out, IS_JMP_CMD, IS_RDY);
  and and_16 (and_16_out, IS_SKIP, STOP_SKIP);
  assign NEXT_STATE = and_13_out ? 5'b10100 : 5'bz;  // Controlled_Buffer controlled_buffer_24
  assign NEXT_STATE = and_14_out ? 5'b10101 : 5'bz;  // Controlled_Buffer controlled_buffer_25
  assign NEXT_STATE = and_15_out ? 5'b10111 : 5'bz;  // Controlled_Buffer controlled_buffer_26
  assign TAPE_NEXT = IS_SKIP ? CLK : 1'bz;  // Controlled_Buffer controlled_buffer_27
  assign NEXT_STATE = and_16_out ? 5'b10010 : 5'bz;  // Controlled_Buffer controlled_buffer_28
  Comparator #(.width(3), .mode("unsigned")) comparator_2 (
    .a(CUR_BF[2:0]), .b(3'b000), .eq(comparator_2_eq));  // open: gt, lt
  not not_7 (not_7_out, CUR_BF[3]);
  Comparator #(.width(3), .mode("unsigned")) comparator_3 (
    .a(CUR_BF[2:0]), .b(3'b001), .eq(IS_WHILE_CMD));  // open: gt, lt
  buf buffer_2 (IS_SIMPLE_CMD, CUR_BF[1]);
  Comparator #(.width(3), .mode("unsigned")) comparator_4 (
    .a(CUR_BF[2:0]), .b(3'b100), .eq(IS_OUT_CMD));  // open: gt, lt
  Comparator #(.width(3), .mode("unsigned")) comparator_5 (
    .a(CUR_BF[2:0]), .b(3'b101), .eq(IS_IN_CMD));  // open: gt, lt
  buf buffer_3 (IS_STOP_CMD, CUR_BF[3]);
  or or_3 (IS_LIKE_JMP_CMD, IS_JMP_CMD, IS_WHILE_CMD);
  Pull_Resistor pull_resistor_2 (.node(HAS_CHAR));
  Hex_Digit_Display hex_digit_display_3 (.value({1'b0, CMD}));  // open: dp
  assign NEXT_STATE = IS_NEXT ? 5'b10000 : 5'bz;  // Controlled_Buffer controlled_buffer_29
  assign TAPE_NEXT = IS_NEXT ? CLK : 1'bz;  // Controlled_Buffer controlled_buffer_30
  and and_17 (IS_JMP_CMD, comparator_2_eq, not_7_out);
  D_Flip_Flop d_ff_2 (.Q(IS_ON), .preset(TURN_ON), .reset(IS_STOP));  // open: clk, D, Qn, en
  assign NEXT_STATE = IS_INIT2 ? 5'b00011 : 5'bz;  // Controlled_Buffer controlled_buffer_31
  assign CELL_CLK = IS_INIT2 ? CLK : 1'bz;  // Controlled_Buffer controlled_buffer_32
  assign NEXT_STATE = CLEAR_ACT ? 5'b10000 : 5'bz;  // Controlled_Buffer controlled_buffer_33
  assign NEXT_CMD = CLEAR_ACT ? 3'b000 : 3'bz;  // Controlled_Buffer controlled_buffer_34
  assign NEXT_STATE = IS_WHGET ? 5'b11010 : 5'bz;  // Controlled_Buffer controlled_buffer_35
  assign CELL_CLK = IS_WHGET ? CLK : 1'bz;  // Controlled_Buffer controlled_buffer_36
  Pull_Resistor pull_resistor_3 (.node(CELL_ZERO));
  Comparator #(.mode("unsigned")) comparator_6 (.a(DATA_FROM_CELL), .b({8{1'b0}}), .eq(CELL_ZERO));  // open: gt, lt
  not not_8 (not_8_out, IS_LIKE_JMP_CMD);
  and and_18 (and_18_out, IS_IN_CMD, HAS_CHAR, IS_RDY);
  and and_19 (IS_STOP, CUR_BF[3], IS_RDY);
  and and_20 (and_20_out, not_8_out, IS_RDY);
  assign NEXT_CMD = and_20_out ? CUR_BF[2:0] : 3'bz;  // Controlled_Buffer controlled_buffer_37
  assign NEXT_TO_CELL = and_18_out ? {1'b0, CHAR} : 8'bz;  // Controlled_Buffer controlled_buffer_38
  assign NEXT_STATE = IS_STOP ? {5{1'b0}} : 5'bz;  // Controlled_Buffer controlled_buffer_39
  assign TAPE_PREV = IS_JMP ? CLK : 1'bz;  // Controlled_Buffer controlled_buffer_40
  and and_21 (and_21_out, IS_JMP, STOP_SKIP);
  assign NEXT_STATE = and_21_out ? 5'b10000 : 5'bz;  // Controlled_Buffer controlled_buffer_41
  assign NEXT_STATE = IS_EXECR ? 5'b10110 : 5'bz;  // Controlled_Buffer controlled_buffer_42
  assign CELL_CLK = IS_EXECR ? CLK : 1'bz;  // Controlled_Buffer controlled_buffer_43

  // Other names for the same wires on the sheet: CELL_CMD[2:0] = CMD; CHAR_t[6:0] = CHAR;
  //   CUR_BF_CMD[2:0] = CUR_BF[2:0]; STOP_FLAG = CUR_BF[3]; CUR_STATE[4] = IS_INITED; STATE_INITED = IS_INITED;
  //   DISP_t[6:0] = DISP; FROM_CELL[7:0] = DATA_FROM_CELL; IS_INIT5 = CLEAR_ACT; IS_INIT1 = TAPE_RST;
  //   SET_ACT = TAPE_RST; TO_CELL[7:0] = DATA_TO_CELL
endmodule

// memcell64
module cell64 (
  input  IS_TAIL,
  input  IS_HEAD,
  input  IS_ACTIVE_RIGHT,
  input  IS_ACTIVE_LEFT,
  input  [7:0] DATA_IN,
  input  [7:0] DATA_OUT,
  input  [2:0] CMD,
  input  CLK,
  output SET_TAIL,
  output SET_HEAD,
  output IS_ACTIVE,
  output IS_ACTIVE_2,
  output [7:0] DATA_IN_2,
  output [7:0] DATA_OUT_2,
  output [2:0] CMD_2,
  output CLK_2,
  output [31:0] DBGROW0_3,
  output [31:0] DBGROW4_7
);

  wire cell_1_clk_2, cell_1_is_active_2, cell_1_set_head, cell_2_clk_2, cell_2_is_active_2, cell_2_set_head,
       cell_3_clk_2, cell_3_is_active_2, cell_3_set_head, cell_4_clk_2, cell_4_is_active_2, cell_4_set_head,
       cell_5_clk_2, cell_5_is_active_2, cell_5_set_head, cell_6_clk_2, cell_6_is_active_2, cell_6_set_head,
       cell_7_clk_2, cell_7_is_active_2, cell_7_set_head, cell_8_clk_2, cell_8_is_active_2, cell_8_set_head,
       cell_9_clk_2, cell_9_is_active, cell_9_is_active_2, cell_9_set_head, cell_9_set_tail, cell_10_clk_2,
       cell_10_is_active, cell_10_is_active_2, cell_10_set_head, cell_10_set_tail, cell_11_clk_2,
       cell_11_is_active, cell_11_is_active_2, cell_11_set_head, cell_11_set_tail, cell_12_clk_2,
       cell_12_is_active, cell_12_is_active_2, cell_12_set_head, cell_12_set_tail, cell_13_clk_2,
       cell_13_is_active, cell_13_is_active_2, cell_13_set_head, cell_13_set_tail, cell_14_clk_2,
       cell_14_is_active, cell_14_is_active_2, cell_14_set_head, cell_14_set_tail, cell_15_clk_2,
       cell_15_is_active, cell_15_is_active_2, cell_15_set_head, cell_15_set_tail, cell_16_clk_2,
       cell_16_is_active, cell_16_is_active_2, cell_16_set_head, cell_16_set_tail, cell_17_clk_2,
       cell_17_is_active, cell_17_is_active_2, cell_17_set_head, cell_17_set_tail, cell_18_clk_2,
       cell_18_is_active, cell_18_is_active_2, cell_18_set_head, cell_18_set_tail, cell_19_clk_2,
       cell_19_is_active, cell_19_is_active_2, cell_19_set_head, cell_19_set_tail, cell_20_clk_2,
       cell_20_is_active, cell_20_is_active_2, cell_20_set_head, cell_20_set_tail, cell_21_clk_2,
       cell_21_is_active, cell_21_is_active_2, cell_21_set_head, cell_21_set_tail, cell_22_clk_2,
       cell_22_is_active, cell_22_is_active_2, cell_22_set_head, cell_22_set_tail, cell_23_clk_2,
       cell_23_is_active, cell_23_is_active_2, cell_23_set_head, cell_23_set_tail, cell_24_clk_2,
       cell_24_is_active, cell_24_is_active_2, cell_24_set_head, cell_24_set_tail, cell_25_clk_2,
       cell_25_is_active, cell_25_is_active_2, cell_25_set_head, cell_25_set_tail, cell_26_clk_2,
       cell_26_is_active, cell_26_is_active_2, cell_26_set_head, cell_26_set_tail, cell_27_clk_2,
       cell_27_is_active, cell_27_is_active_2, cell_27_set_head, cell_27_set_tail, cell_28_clk_2,
       cell_28_is_active, cell_28_is_active_2, cell_28_set_head, cell_28_set_tail, cell_29_clk_2,
       cell_29_is_active, cell_29_is_active_2, cell_29_set_head, cell_29_set_tail, cell_30_clk_2,
       cell_30_is_active, cell_30_is_active_2, cell_30_set_head, cell_30_set_tail, cell_31_clk_2,
       cell_31_is_active, cell_31_is_active_2, cell_31_set_head, cell_31_set_tail, cell_32_clk_2,
       cell_32_is_active, cell_32_is_active_2, cell_32_set_head, cell_32_set_tail, cell_33_clk_2,
       cell_33_is_active, cell_33_is_active_2, cell_33_set_head, cell_33_set_tail, cell_34_clk_2,
       cell_34_is_active, cell_34_is_active_2, cell_34_set_head, cell_34_set_tail, cell_35_clk_2,
       cell_35_is_active, cell_35_is_active_2, cell_35_set_head, cell_35_set_tail, cell_36_clk_2,
       cell_36_is_active, cell_36_is_active_2, cell_36_set_head, cell_36_set_tail, cell_37_clk_2,
       cell_37_is_active, cell_37_is_active_2, cell_37_set_head, cell_37_set_tail, cell_38_clk_2,
       cell_38_is_active, cell_38_is_active_2, cell_38_set_head, cell_38_set_tail, cell_39_clk_2,
       cell_39_is_active, cell_39_is_active_2, cell_39_set_head, cell_39_set_tail, cell_40_clk_2,
       cell_40_is_active, cell_40_is_active_2, cell_40_set_head, cell_40_set_tail, cell_41_clk_2,
       cell_41_is_active, cell_41_is_active_2, cell_41_set_head, cell_41_set_tail, cell_42_clk_2,
       cell_42_is_active, cell_42_is_active_2, cell_42_set_head, cell_42_set_tail, cell_43_clk_2,
       cell_43_is_active, cell_43_is_active_2, cell_43_set_head, cell_43_set_tail, cell_44_clk_2,
       cell_44_is_active, cell_44_is_active_2, cell_44_set_head, cell_44_set_tail, cell_45_clk_2,
       cell_45_is_active, cell_45_is_active_2, cell_45_set_head, cell_45_set_tail, cell_46_clk_2,
       cell_46_is_active, cell_46_is_active_2, cell_46_set_head, cell_46_set_tail, cell_47_clk_2,
       cell_47_is_active, cell_47_is_active_2, cell_47_set_head, cell_47_set_tail, cell_48_clk_2,
       cell_48_is_active, cell_48_is_active_2, cell_48_set_head, cell_48_set_tail, cell_49_clk_2,
       cell_49_is_active, cell_49_is_active_2, cell_49_set_head, cell_49_set_tail, cell_50_clk_2,
       cell_50_is_active, cell_50_is_active_2, cell_50_set_head, cell_50_set_tail, cell_51_clk_2,
       cell_51_is_active, cell_51_is_active_2, cell_51_set_head, cell_51_set_tail, cell_52_clk_2,
       cell_52_is_active, cell_52_is_active_2, cell_52_set_head, cell_52_set_tail, cell_53_clk_2,
       cell_53_is_active, cell_53_is_active_2, cell_53_set_head, cell_53_set_tail, cell_54_clk_2,
       cell_54_is_active, cell_54_is_active_2, cell_54_set_head, cell_54_set_tail, cell_55_clk_2,
       cell_55_is_active, cell_55_is_active_2, cell_55_set_head, cell_55_set_tail, cell_56_clk_2,
       cell_56_is_active, cell_56_is_active_2, cell_56_set_head, cell_56_set_tail, cell_57_is_active,
       cell_57_set_tail, cell_58_is_active, cell_58_set_tail, cell_59_is_active, cell_59_set_tail,
       cell_60_is_active, cell_60_set_tail, cell_61_is_active, cell_61_set_tail, cell_62_is_active,
       cell_62_set_tail, cell_63_is_active, cell_63_set_tail, cell_64_is_active, cell_64_set_tail;
  wire [2:0] cell_1_cmd_2, cell_1_dbg_led, cell_2_cmd_2, cell_2_dbg_led, cell_3_cmd_2, cell_3_dbg_led,
       cell_4_cmd_2, cell_4_dbg_led, cell_5_cmd_2, cell_5_dbg_led, cell_6_cmd_2, cell_6_dbg_led,
       cell_7_cmd_2, cell_7_dbg_led, cell_8_cmd_2, cell_8_dbg_led, cell_9_cmd_2, cell_9_dbg_led,
       cell_10_cmd_2, cell_10_dbg_led, cell_11_cmd_2, cell_11_dbg_led, cell_12_cmd_2, cell_12_dbg_led,
       cell_13_cmd_2, cell_13_dbg_led, cell_14_cmd_2, cell_14_dbg_led, cell_15_cmd_2, cell_15_dbg_led,
       cell_16_cmd_2, cell_16_dbg_led, cell_17_cmd_2, cell_17_dbg_led, cell_18_cmd_2, cell_18_dbg_led,
       cell_19_cmd_2, cell_19_dbg_led, cell_20_cmd_2, cell_20_dbg_led, cell_21_cmd_2, cell_21_dbg_led,
       cell_22_cmd_2, cell_22_dbg_led, cell_23_cmd_2, cell_23_dbg_led, cell_24_cmd_2, cell_24_dbg_led,
       cell_25_cmd_2, cell_25_dbg_led, cell_26_cmd_2, cell_26_dbg_led, cell_27_cmd_2, cell_27_dbg_led,
       cell_28_cmd_2, cell_28_dbg_led, cell_29_cmd_2, cell_29_dbg_led, cell_30_cmd_2, cell_30_dbg_led,
       cell_31_cmd_2, cell_31_dbg_led, cell_32_cmd_2, cell_32_dbg_led, cell_33_cmd_2, cell_33_dbg_led,
       cell_34_cmd_2, cell_34_dbg_led, cell_35_cmd_2, cell_35_dbg_led, cell_36_cmd_2, cell_36_dbg_led,
       cell_37_cmd_2, cell_37_dbg_led, cell_38_cmd_2, cell_38_dbg_led, cell_39_cmd_2, cell_39_dbg_led,
       cell_40_cmd_2, cell_40_dbg_led, cell_41_cmd_2, cell_41_dbg_led, cell_42_cmd_2, cell_42_dbg_led,
       cell_43_cmd_2, cell_43_dbg_led, cell_44_cmd_2, cell_44_dbg_led, cell_45_cmd_2, cell_45_dbg_led,
       cell_46_cmd_2, cell_46_dbg_led, cell_47_cmd_2, cell_47_dbg_led, cell_48_cmd_2, cell_48_dbg_led,
       cell_49_cmd_2, cell_49_dbg_led, cell_50_cmd_2, cell_50_dbg_led, cell_51_cmd_2, cell_51_dbg_led,
       cell_52_cmd_2, cell_52_dbg_led, cell_53_cmd_2, cell_53_dbg_led, cell_54_cmd_2, cell_54_dbg_led,
       cell_55_cmd_2, cell_55_dbg_led, cell_56_cmd_2, cell_56_dbg_led, cell_57_dbg_led, cell_58_dbg_led,
       cell_59_dbg_led, cell_60_dbg_led, cell_61_dbg_led, cell_62_dbg_led, cell_63_dbg_led, cell_64_dbg_led;
  wire [3:0] cell_1_dbg_mem, cell_1_dbg_mem_2, cell_2_dbg_mem, cell_2_dbg_mem_2, cell_8_dbg_mem,
       cell_8_dbg_mem_2, cell_10_dbg_mem, cell_10_dbg_mem_2, cell_11_dbg_mem, cell_11_dbg_mem_2,
       cell_12_dbg_mem, cell_12_dbg_mem_2, cell_20_dbg_mem, cell_20_dbg_mem_2, cell_21_dbg_mem,
       cell_21_dbg_mem_2, cell_22_dbg_mem, cell_22_dbg_mem_2, cell_25_dbg_mem, cell_25_dbg_mem_2,
       cell_31_dbg_mem, cell_31_dbg_mem_2, cell_32_dbg_mem, cell_32_dbg_mem_2, cell_33_dbg_mem,
       cell_33_dbg_mem_2, cell_34_dbg_mem, cell_34_dbg_mem_2, cell_35_dbg_mem, cell_35_dbg_mem_2,
       cell_43_dbg_mem, cell_43_dbg_mem_2, cell_44_dbg_mem, cell_44_dbg_mem_2, cell_45_dbg_mem,
       cell_45_dbg_mem_2, cell_53_dbg_mem, cell_53_dbg_mem_2, cell_54_dbg_mem, cell_54_dbg_mem_2,
       cell_55_dbg_mem, cell_55_dbg_mem_2, cell_57_dbg_mem, cell_57_dbg_mem_2, cell_58_dbg_mem,
       cell_58_dbg_mem_2, cell_59_dbg_mem, cell_59_dbg_mem_2, cell_60_dbg_mem, cell_60_dbg_mem_2,
       cell_61_dbg_mem, cell_61_dbg_mem_2, cell_62_dbg_mem, cell_62_dbg_mem_2, cell_63_dbg_mem,
       cell_63_dbg_mem_2, cell_64_dbg_mem, cell_64_dbg_mem_2;
  wire [7:0] cell_1_data_in_2, cell_2_data_in_2, cell_3_data_in_2, cell_3_dbg_mem, cell_4_data_in_2,
       cell_4_dbg_mem, cell_5_data_in_2, cell_5_dbg_mem, cell_6_data_in_2, cell_6_dbg_mem, cell_7_data_in_2,
       cell_7_dbg_mem, cell_8_data_in_2, cell_9_data_in_2, cell_9_data_out_2, cell_9_dbg_mem,
       cell_10_data_in_2, cell_10_data_out_2, cell_11_data_in_2, cell_11_data_out_2, cell_12_data_in_2,
       cell_12_data_out_2, cell_13_data_in_2, cell_13_data_out_2, cell_13_dbg_mem, cell_14_data_in_2,
       cell_14_data_out_2, cell_14_dbg_mem, cell_15_data_in_2, cell_15_data_out_2, cell_15_dbg_mem,
       cell_16_data_in_2, cell_16_data_out_2, cell_16_dbg_mem, cell_17_data_in_2, cell_17_data_out_2,
       cell_17_dbg_mem, cell_18_data_in_2, cell_18_data_out_2, cell_18_dbg_mem, cell_19_data_in_2,
       cell_19_data_out_2, cell_19_dbg_mem, cell_20_data_in_2, cell_20_data_out_2, cell_21_data_in_2,
       cell_21_data_out_2, cell_22_data_in_2, cell_22_data_out_2, cell_23_data_in_2, cell_23_data_out_2,
       cell_23_dbg_mem, cell_24_data_in_2, cell_24_data_out_2, cell_24_dbg_mem, cell_25_data_in_2,
       cell_25_data_out_2, cell_26_data_in_2, cell_26_data_out_2, cell_26_dbg_mem, cell_27_data_in_2,
       cell_27_data_out_2, cell_27_dbg_mem, cell_28_data_in_2, cell_28_data_out_2, cell_28_dbg_mem,
       cell_29_data_in_2, cell_29_data_out_2, cell_29_dbg_mem, cell_30_data_in_2, cell_30_data_out_2,
       cell_30_dbg_mem, cell_31_data_in_2, cell_31_data_out_2, cell_32_data_in_2, cell_32_data_out_2,
       cell_33_data_in_2, cell_33_data_out_2, cell_34_data_in_2, cell_34_data_out_2, cell_35_data_in_2,
       cell_35_data_out_2, cell_36_data_in_2, cell_36_data_out_2, cell_36_dbg_mem, cell_37_data_in_2,
       cell_37_data_out_2, cell_37_dbg_mem, cell_38_data_in_2, cell_38_data_out_2, cell_38_dbg_mem,
       cell_39_data_in_2, cell_39_data_out_2, cell_39_dbg_mem, cell_40_data_in_2, cell_40_data_out_2,
       cell_40_dbg_mem, cell_41_data_in_2, cell_41_data_out_2, cell_41_dbg_mem, cell_42_data_in_2,
       cell_42_data_out_2, cell_42_dbg_mem, cell_43_data_in_2, cell_43_data_out_2, cell_44_data_in_2,
       cell_44_data_out_2, cell_45_data_in_2, cell_45_data_out_2, cell_46_data_in_2, cell_46_data_out_2,
       cell_46_dbg_mem, cell_47_data_in_2, cell_47_data_out_2, cell_47_dbg_mem, cell_48_data_in_2,
       cell_48_data_out_2, cell_48_dbg_mem, cell_49_data_in_2, cell_49_data_out_2, cell_49_dbg_mem,
       cell_50_data_in_2, cell_50_data_out_2, cell_50_dbg_mem, cell_51_data_in_2, cell_51_data_out_2,
       cell_51_dbg_mem, cell_52_data_in_2, cell_52_data_out_2, cell_52_dbg_mem, cell_53_data_in_2,
       cell_53_data_out_2, cell_54_data_in_2, cell_54_data_out_2, cell_55_data_in_2, cell_55_data_out_2,
       cell_56_data_in_2, cell_56_data_out_2, cell_56_dbg_mem, cell_57_data_out_2, cell_58_data_out_2,
       cell_59_data_out_2, cell_60_data_out_2, cell_61_data_out_2, cell_62_data_out_2, cell_63_data_out_2,
       cell_64_data_out_2;
  wire [23:0] ROW0_ROW1, ROW1_ROW2, ROW2_ROW3, ROW3_ROW4, ROW4_ROW5, ROW5_ROW6, ROW6_ROW7;

  \cell  cell_1 (
    .SET_TAIL(SET_TAIL), .IS_HEAD(IS_HEAD), .IS_ACTIVE(IS_ACTIVE), .IS_ACTIVE_LEFT(IS_ACTIVE_LEFT),
    .DATA_IN(DATA_IN), .DATA_OUT_2(DATA_OUT_2), .CMD(CMD), .CLK(CLK), .IS_TAIL(cell_9_set_tail),
    .SET_HEAD(cell_1_set_head), .IS_ACTIVE_RIGHT(cell_9_is_active), .IS_ACTIVE_2(cell_1_is_active_2),
    .DATA_IN_2(cell_1_data_in_2), .DATA_OUT(cell_9_data_out_2), .CMD_2(cell_1_cmd_2), .CLK_2(cell_1_clk_2),
    .DBG_MEM({cell_1_dbg_mem_2, cell_1_dbg_mem}),
    .DBG_LED({cell_1_dbg_led[2], DBGROW0_3[7], cell_1_dbg_led[0]}));
  Hex_Digit_Display hex_digit_display_1 (.value(cell_1_dbg_mem));  // open: dp
  Hex_Digit_Display hex_digit_display_2 (.value(cell_1_dbg_mem_2));  // open: dp
  \cell  cell_2 (
    .SET_TAIL(ROW0_ROW1[0]), .IS_HEAD(ROW0_ROW1[1]), .IS_ACTIVE(ROW0_ROW1[2]), .IS_ACTIVE_LEFT(ROW0_ROW1[3]),
    .DATA_IN(ROW0_ROW1[11:4]), .DATA_OUT_2(ROW0_ROW1[19:12]), .CMD(ROW0_ROW1[22:20]), .CLK(ROW0_ROW1[23]),
    .IS_TAIL(cell_10_set_tail), .SET_HEAD(cell_2_set_head), .IS_ACTIVE_RIGHT(cell_10_is_active),
    .IS_ACTIVE_2(cell_2_is_active_2), .DATA_IN_2(cell_2_data_in_2), .DATA_OUT(cell_10_data_out_2),
    .CMD_2(cell_2_cmd_2), .CLK_2(cell_2_clk_2), .DBG_MEM({cell_2_dbg_mem_2, cell_2_dbg_mem}),
    .DBG_LED({cell_2_dbg_led[2], DBGROW0_3[15], cell_2_dbg_led[0]}));
  Hex_Digit_Display hex_digit_display_3 (.value(cell_2_dbg_mem));  // open: dp
  Hex_Digit_Display hex_digit_display_4 (.value(cell_2_dbg_mem_2));  // open: dp
  \cell  cell_3 (
    .SET_TAIL(ROW1_ROW2[0]), .IS_HEAD(ROW1_ROW2[1]), .IS_ACTIVE(ROW1_ROW2[2]), .IS_ACTIVE_LEFT(ROW1_ROW2[3]),
    .DATA_IN(ROW1_ROW2[11:4]), .DATA_OUT_2(ROW1_ROW2[19:12]), .CMD(ROW1_ROW2[22:20]), .CLK(ROW1_ROW2[23]),
    .IS_TAIL(cell_11_set_tail), .SET_HEAD(cell_3_set_head), .IS_ACTIVE_RIGHT(cell_11_is_active),
    .IS_ACTIVE_2(cell_3_is_active_2), .DATA_IN_2(cell_3_data_in_2), .DATA_OUT(cell_11_data_out_2),
    .CMD_2(cell_3_cmd_2), .CLK_2(cell_3_clk_2), .DBG_MEM(cell_3_dbg_mem),
    .DBG_LED({cell_3_dbg_led[2], DBGROW0_3[23], cell_3_dbg_led[0]}));
  Hex_Digit_Display hex_digit_display_5 (.value(cell_3_dbg_mem[3:0]));  // open: dp
  Hex_Digit_Display hex_digit_display_6 (.value(cell_3_dbg_mem[7:4]));  // open: dp
  \cell  cell_4 (
    .SET_TAIL(ROW2_ROW3[0]), .IS_HEAD(ROW2_ROW3[1]), .IS_ACTIVE(ROW2_ROW3[2]), .IS_ACTIVE_LEFT(ROW2_ROW3[3]),
    .DATA_IN(ROW2_ROW3[11:4]), .DATA_OUT_2(ROW2_ROW3[19:12]), .CMD(ROW2_ROW3[22:20]), .CLK(ROW2_ROW3[23]),
    .IS_TAIL(cell_12_set_tail), .SET_HEAD(cell_4_set_head), .IS_ACTIVE_RIGHT(cell_12_is_active),
    .IS_ACTIVE_2(cell_4_is_active_2), .DATA_IN_2(cell_4_data_in_2), .DATA_OUT(cell_12_data_out_2),
    .CMD_2(cell_4_cmd_2), .CLK_2(cell_4_clk_2), .DBG_MEM(cell_4_dbg_mem),
    .DBG_LED({cell_4_dbg_led[2], DBGROW0_3[31], cell_4_dbg_led[0]}));
  Hex_Digit_Display hex_digit_display_7 (.value(cell_4_dbg_mem[7:4]));  // open: dp
  Hex_Digit_Display hex_digit_display_8 (.value(cell_4_dbg_mem[3:0]));  // open: dp
  \cell  cell_5 (
    .SET_TAIL(ROW3_ROW4[0]), .IS_HEAD(ROW3_ROW4[1]), .IS_ACTIVE(ROW3_ROW4[2]), .IS_ACTIVE_LEFT(ROW3_ROW4[3]),
    .DATA_IN(ROW3_ROW4[11:4]), .DATA_OUT_2(ROW3_ROW4[19:12]), .CMD(ROW3_ROW4[22:20]), .CLK(ROW3_ROW4[23]),
    .IS_TAIL(cell_13_set_tail), .SET_HEAD(cell_5_set_head), .IS_ACTIVE_RIGHT(cell_13_is_active),
    .IS_ACTIVE_2(cell_5_is_active_2), .DATA_IN_2(cell_5_data_in_2), .DATA_OUT(cell_13_data_out_2),
    .CMD_2(cell_5_cmd_2), .CLK_2(cell_5_clk_2), .DBG_MEM(cell_5_dbg_mem),
    .DBG_LED({cell_5_dbg_led[2], DBGROW4_7[7], cell_5_dbg_led[0]}));
  Hex_Digit_Display hex_digit_display_9 (.value(cell_5_dbg_mem[3:0]));  // open: dp
  Hex_Digit_Display hex_digit_display_10 (.value(cell_5_dbg_mem[7:4]));  // open: dp
  \cell  cell_6 (
    .SET_TAIL(ROW4_ROW5[0]), .IS_HEAD(ROW4_ROW5[1]), .IS_ACTIVE(ROW4_ROW5[2]), .IS_ACTIVE_LEFT(ROW4_ROW5[3]),
    .DATA_IN(ROW4_ROW5[11:4]), .DATA_OUT_2(ROW4_ROW5[19:12]), .CMD(ROW4_ROW5[22:20]), .CLK(ROW4_ROW5[23]),
    .IS_TAIL(cell_14_set_tail), .SET_HEAD(cell_6_set_head), .IS_ACTIVE_RIGHT(cell_14_is_active),
    .IS_ACTIVE_2(cell_6_is_active_2), .DATA_IN_2(cell_6_data_in_2), .DATA_OUT(cell_14_data_out_2),
    .CMD_2(cell_6_cmd_2), .CLK_2(cell_6_clk_2), .DBG_MEM(cell_6_dbg_mem),
    .DBG_LED({cell_6_dbg_led[2], DBGROW4_7[15], cell_6_dbg_led[0]}));
  Hex_Digit_Display hex_digit_display_11 (.value(cell_6_dbg_mem[7:4]));  // open: dp
  Hex_Digit_Display hex_digit_display_12 (.value(cell_6_dbg_mem[3:0]));  // open: dp
  \cell  cell_7 (
    .SET_TAIL(ROW5_ROW6[0]), .IS_HEAD(ROW5_ROW6[1]), .IS_ACTIVE(ROW5_ROW6[2]), .IS_ACTIVE_LEFT(ROW5_ROW6[3]),
    .DATA_IN(ROW5_ROW6[11:4]), .DATA_OUT_2(ROW5_ROW6[19:12]), .CMD(ROW5_ROW6[22:20]), .CLK(ROW5_ROW6[23]),
    .IS_TAIL(cell_15_set_tail), .SET_HEAD(cell_7_set_head), .IS_ACTIVE_RIGHT(cell_15_is_active),
    .IS_ACTIVE_2(cell_7_is_active_2), .DATA_IN_2(cell_7_data_in_2), .DATA_OUT(cell_15_data_out_2),
    .CMD_2(cell_7_cmd_2), .CLK_2(cell_7_clk_2), .DBG_MEM(cell_7_dbg_mem),
    .DBG_LED({cell_7_dbg_led[2], DBGROW4_7[23], cell_7_dbg_led[0]}));
  Hex_Digit_Display hex_digit_display_13 (.value(cell_7_dbg_mem[7:4]));  // open: dp
  Hex_Digit_Display hex_digit_display_14 (.value(cell_7_dbg_mem[3:0]));  // open: dp
  \cell  cell_8 (
    .SET_TAIL(ROW6_ROW7[0]), .IS_HEAD(ROW6_ROW7[1]), .IS_ACTIVE(ROW6_ROW7[2]), .IS_ACTIVE_LEFT(ROW6_ROW7[3]),
    .DATA_IN(ROW6_ROW7[11:4]), .DATA_OUT_2(ROW6_ROW7[19:12]), .CMD(ROW6_ROW7[22:20]), .CLK(ROW6_ROW7[23]),
    .IS_TAIL(cell_16_set_tail), .SET_HEAD(cell_8_set_head), .IS_ACTIVE_RIGHT(cell_16_is_active),
    .IS_ACTIVE_2(cell_8_is_active_2), .DATA_IN_2(cell_8_data_in_2), .DATA_OUT(cell_16_data_out_2),
    .CMD_2(cell_8_cmd_2), .CLK_2(cell_8_clk_2), .DBG_MEM({cell_8_dbg_mem_2, cell_8_dbg_mem}),
    .DBG_LED({cell_8_dbg_led[2], DBGROW4_7[31], cell_8_dbg_led[0]}));
  Hex_Digit_Display hex_digit_display_15 (.value(cell_8_dbg_mem_2));  // open: dp
  Hex_Digit_Display hex_digit_display_16 (.value(cell_8_dbg_mem));  // open: dp
  \cell  cell_9 (
    .SET_TAIL(cell_9_set_tail), .IS_HEAD(cell_1_set_head), .IS_ACTIVE(cell_9_is_active),
    .IS_ACTIVE_LEFT(cell_1_is_active_2), .DATA_IN(cell_1_data_in_2), .DATA_OUT_2(cell_9_data_out_2),
    .CMD(cell_1_cmd_2), .CLK(cell_1_clk_2), .IS_TAIL(cell_17_set_tail), .SET_HEAD(cell_9_set_head),
    .IS_ACTIVE_RIGHT(cell_17_is_active), .IS_ACTIVE_2(cell_9_is_active_2), .DATA_IN_2(cell_9_data_in_2),
    .DATA_OUT(cell_17_data_out_2), .CMD_2(cell_9_cmd_2), .CLK_2(cell_9_clk_2), .DBG_MEM(cell_9_dbg_mem),
    .DBG_LED({cell_9_dbg_led[2], DBGROW0_3[6], cell_9_dbg_led[0]}));
  Hex_Digit_Display hex_digit_display_17 (.value(cell_9_dbg_mem[3:0]));  // open: dp
  Hex_Digit_Display hex_digit_display_18 (.value(cell_9_dbg_mem[7:4]));  // open: dp
  \cell  cell_10 (
    .SET_TAIL(cell_10_set_tail), .IS_HEAD(cell_2_set_head), .IS_ACTIVE(cell_10_is_active),
    .IS_ACTIVE_LEFT(cell_2_is_active_2), .DATA_IN(cell_2_data_in_2), .DATA_OUT_2(cell_10_data_out_2),
    .CMD(cell_2_cmd_2), .CLK(cell_2_clk_2), .IS_TAIL(cell_18_set_tail), .SET_HEAD(cell_10_set_head),
    .IS_ACTIVE_RIGHT(cell_18_is_active), .IS_ACTIVE_2(cell_10_is_active_2), .DATA_IN_2(cell_10_data_in_2),
    .DATA_OUT(cell_18_data_out_2), .CMD_2(cell_10_cmd_2), .CLK_2(cell_10_clk_2),
    .DBG_MEM({cell_10_dbg_mem_2, cell_10_dbg_mem}),
    .DBG_LED({cell_10_dbg_led[2], DBGROW0_3[14], cell_10_dbg_led[0]}));
  Hex_Digit_Display hex_digit_display_19 (.value(cell_10_dbg_mem));  // open: dp
  Hex_Digit_Display hex_digit_display_20 (.value(cell_10_dbg_mem_2));  // open: dp
  \cell  cell_11 (
    .SET_TAIL(cell_11_set_tail), .IS_HEAD(cell_3_set_head), .IS_ACTIVE(cell_11_is_active),
    .IS_ACTIVE_LEFT(cell_3_is_active_2), .DATA_IN(cell_3_data_in_2), .DATA_OUT_2(cell_11_data_out_2),
    .CMD(cell_3_cmd_2), .CLK(cell_3_clk_2), .IS_TAIL(cell_19_set_tail), .SET_HEAD(cell_11_set_head),
    .IS_ACTIVE_RIGHT(cell_19_is_active), .IS_ACTIVE_2(cell_11_is_active_2), .DATA_IN_2(cell_11_data_in_2),
    .DATA_OUT(cell_19_data_out_2), .CMD_2(cell_11_cmd_2), .CLK_2(cell_11_clk_2),
    .DBG_MEM({cell_11_dbg_mem_2, cell_11_dbg_mem}),
    .DBG_LED({cell_11_dbg_led[2], DBGROW0_3[22], cell_11_dbg_led[0]}));
  Hex_Digit_Display hex_digit_display_21 (.value(cell_11_dbg_mem));  // open: dp
  Hex_Digit_Display hex_digit_display_22 (.value(cell_11_dbg_mem_2));  // open: dp
  \cell  cell_12 (
    .SET_TAIL(cell_12_set_tail), .IS_HEAD(cell_4_set_head), .IS_ACTIVE(cell_12_is_active),
    .IS_ACTIVE_LEFT(cell_4_is_active_2), .DATA_IN(cell_4_data_in_2), .DATA_OUT_2(cell_12_data_out_2),
    .CMD(cell_4_cmd_2), .CLK(cell_4_clk_2), .IS_TAIL(cell_20_set_tail), .SET_HEAD(cell_12_set_head),
    .IS_ACTIVE_RIGHT(cell_20_is_active), .IS_ACTIVE_2(cell_12_is_active_2), .DATA_IN_2(cell_12_data_in_2),
    .DATA_OUT(cell_20_data_out_2), .CMD_2(cell_12_cmd_2), .CLK_2(cell_12_clk_2),
    .DBG_MEM({cell_12_dbg_mem_2, cell_12_dbg_mem}),
    .DBG_LED({cell_12_dbg_led[2], DBGROW0_3[30], cell_12_dbg_led[0]}));
  Hex_Digit_Display hex_digit_display_23 (.value(cell_12_dbg_mem_2));  // open: dp
  Hex_Digit_Display hex_digit_display_24 (.value(cell_12_dbg_mem));  // open: dp
  \cell  cell_13 (
    .SET_TAIL(cell_13_set_tail), .IS_HEAD(cell_5_set_head), .IS_ACTIVE(cell_13_is_active),
    .IS_ACTIVE_LEFT(cell_5_is_active_2), .DATA_IN(cell_5_data_in_2), .DATA_OUT_2(cell_13_data_out_2),
    .CMD(cell_5_cmd_2), .CLK(cell_5_clk_2), .IS_TAIL(cell_21_set_tail), .SET_HEAD(cell_13_set_head),
    .IS_ACTIVE_RIGHT(cell_21_is_active), .IS_ACTIVE_2(cell_13_is_active_2), .DATA_IN_2(cell_13_data_in_2),
    .DATA_OUT(cell_21_data_out_2), .CMD_2(cell_13_cmd_2), .CLK_2(cell_13_clk_2), .DBG_MEM(cell_13_dbg_mem),
    .DBG_LED({cell_13_dbg_led[2], DBGROW4_7[6], cell_13_dbg_led[0]}));
  Hex_Digit_Display hex_digit_display_25 (.value(cell_13_dbg_mem[3:0]));  // open: dp
  Hex_Digit_Display hex_digit_display_26 (.value(cell_13_dbg_mem[7:4]));  // open: dp
  \cell  cell_14 (
    .SET_TAIL(cell_14_set_tail), .IS_HEAD(cell_6_set_head), .IS_ACTIVE(cell_14_is_active),
    .IS_ACTIVE_LEFT(cell_6_is_active_2), .DATA_IN(cell_6_data_in_2), .DATA_OUT_2(cell_14_data_out_2),
    .CMD(cell_6_cmd_2), .CLK(cell_6_clk_2), .IS_TAIL(cell_22_set_tail), .SET_HEAD(cell_14_set_head),
    .IS_ACTIVE_RIGHT(cell_22_is_active), .IS_ACTIVE_2(cell_14_is_active_2), .DATA_IN_2(cell_14_data_in_2),
    .DATA_OUT(cell_22_data_out_2), .CMD_2(cell_14_cmd_2), .CLK_2(cell_14_clk_2), .DBG_MEM(cell_14_dbg_mem),
    .DBG_LED({cell_14_dbg_led[2], DBGROW4_7[14], cell_14_dbg_led[0]}));
  Hex_Digit_Display hex_digit_display_27 (.value(cell_14_dbg_mem[3:0]));  // open: dp
  Hex_Digit_Display hex_digit_display_28 (.value(cell_14_dbg_mem[7:4]));  // open: dp
  \cell  cell_15 (
    .SET_TAIL(cell_15_set_tail), .IS_HEAD(cell_7_set_head), .IS_ACTIVE(cell_15_is_active),
    .IS_ACTIVE_LEFT(cell_7_is_active_2), .DATA_IN(cell_7_data_in_2), .DATA_OUT_2(cell_15_data_out_2),
    .CMD(cell_7_cmd_2), .CLK(cell_7_clk_2), .IS_TAIL(cell_23_set_tail), .SET_HEAD(cell_15_set_head),
    .IS_ACTIVE_RIGHT(cell_23_is_active), .IS_ACTIVE_2(cell_15_is_active_2), .DATA_IN_2(cell_15_data_in_2),
    .DATA_OUT(cell_23_data_out_2), .CMD_2(cell_15_cmd_2), .CLK_2(cell_15_clk_2), .DBG_MEM(cell_15_dbg_mem),
    .DBG_LED({cell_15_dbg_led[2], DBGROW4_7[22], cell_15_dbg_led[0]}));
  Hex_Digit_Display hex_digit_display_29 (.value(cell_15_dbg_mem[7:4]));  // open: dp
  Hex_Digit_Display hex_digit_display_30 (.value(cell_15_dbg_mem[3:0]));  // open: dp
  \cell  cell_16 (
    .SET_TAIL(cell_16_set_tail), .IS_HEAD(cell_8_set_head), .IS_ACTIVE(cell_16_is_active),
    .IS_ACTIVE_LEFT(cell_8_is_active_2), .DATA_IN(cell_8_data_in_2), .DATA_OUT_2(cell_16_data_out_2),
    .CMD(cell_8_cmd_2), .CLK(cell_8_clk_2), .IS_TAIL(cell_24_set_tail), .SET_HEAD(cell_16_set_head),
    .IS_ACTIVE_RIGHT(cell_24_is_active), .IS_ACTIVE_2(cell_16_is_active_2), .DATA_IN_2(cell_16_data_in_2),
    .DATA_OUT(cell_24_data_out_2), .CMD_2(cell_16_cmd_2), .CLK_2(cell_16_clk_2), .DBG_MEM(cell_16_dbg_mem),
    .DBG_LED({cell_16_dbg_led[2], DBGROW4_7[30], cell_16_dbg_led[0]}));
  Hex_Digit_Display hex_digit_display_31 (.value(cell_16_dbg_mem[3:0]));  // open: dp
  Hex_Digit_Display hex_digit_display_32 (.value(cell_16_dbg_mem[7:4]));  // open: dp
  Hex_Digit_Display hex_digit_display_33 (.value(cell_17_dbg_mem[7:4]));  // open: dp
  Hex_Digit_Display hex_digit_display_34 (.value(cell_18_dbg_mem[7:4]));  // open: dp
  Hex_Digit_Display hex_digit_display_35 (.value(cell_19_dbg_mem[7:4]));  // open: dp
  Hex_Digit_Display hex_digit_display_36 (.value(cell_20_dbg_mem_2));  // open: dp
  Hex_Digit_Display hex_digit_display_37 (.value(cell_21_dbg_mem_2));  // open: dp
  Hex_Digit_Display hex_digit_display_38 (.value(cell_22_dbg_mem_2));  // open: dp
  Hex_Digit_Display hex_digit_display_39 (.value(cell_23_dbg_mem[7:4]));  // open: dp
  Hex_Digit_Display hex_digit_display_40 (.value(cell_24_dbg_mem[7:4]));  // open: dp
  \cell  cell_17 (
    .SET_TAIL(cell_17_set_tail), .IS_HEAD(cell_9_set_head), .IS_ACTIVE(cell_17_is_active),
    .IS_ACTIVE_LEFT(cell_9_is_active_2), .DATA_IN(cell_9_data_in_2), .DATA_OUT_2(cell_17_data_out_2),
    .CMD(cell_9_cmd_2), .CLK(cell_9_clk_2), .IS_TAIL(cell_25_set_tail), .SET_HEAD(cell_17_set_head),
    .IS_ACTIVE_RIGHT(cell_25_is_active), .IS_ACTIVE_2(cell_17_is_active_2), .DATA_IN_2(cell_17_data_in_2),
    .DATA_OUT(cell_25_data_out_2), .CMD_2(cell_17_cmd_2), .CLK_2(cell_17_clk_2), .DBG_MEM(cell_17_dbg_mem),
    .DBG_LED({cell_17_dbg_led[2], DBGROW0_3[5], cell_17_dbg_led[0]}));
  Hex_Digit_Display hex_digit_display_41 (.value(cell_17_dbg_mem[3:0]));  // open: dp
  \cell  cell_18 (
    .SET_TAIL(cell_18_set_tail), .IS_HEAD(cell_10_set_head), .IS_ACTIVE(cell_18_is_active),
    .IS_ACTIVE_LEFT(cell_10_is_active_2), .DATA_IN(cell_10_data_in_2), .DATA_OUT_2(cell_18_data_out_2),
    .CMD(cell_10_cmd_2), .CLK(cell_10_clk_2), .IS_TAIL(cell_26_set_tail), .SET_HEAD(cell_18_set_head),
    .IS_ACTIVE_RIGHT(cell_26_is_active), .IS_ACTIVE_2(cell_18_is_active_2), .DATA_IN_2(cell_18_data_in_2),
    .DATA_OUT(cell_26_data_out_2), .CMD_2(cell_18_cmd_2), .CLK_2(cell_18_clk_2), .DBG_MEM(cell_18_dbg_mem),
    .DBG_LED({cell_18_dbg_led[2], DBGROW0_3[13], cell_18_dbg_led[0]}));
  Hex_Digit_Display hex_digit_display_42 (.value(cell_18_dbg_mem[3:0]));  // open: dp
  \cell  cell_19 (
    .SET_TAIL(cell_19_set_tail), .IS_HEAD(cell_11_set_head), .IS_ACTIVE(cell_19_is_active),
    .IS_ACTIVE_LEFT(cell_11_is_active_2), .DATA_IN(cell_11_data_in_2), .DATA_OUT_2(cell_19_data_out_2),
    .CMD(cell_11_cmd_2), .CLK(cell_11_clk_2), .IS_TAIL(cell_27_set_tail), .SET_HEAD(cell_19_set_head),
    .IS_ACTIVE_RIGHT(cell_27_is_active), .IS_ACTIVE_2(cell_19_is_active_2), .DATA_IN_2(cell_19_data_in_2),
    .DATA_OUT(cell_27_data_out_2), .CMD_2(cell_19_cmd_2), .CLK_2(cell_19_clk_2), .DBG_MEM(cell_19_dbg_mem),
    .DBG_LED({cell_19_dbg_led[2], DBGROW0_3[21], cell_19_dbg_led[0]}));
  Hex_Digit_Display hex_digit_display_43 (.value(cell_19_dbg_mem[3:0]));  // open: dp
  \cell  cell_20 (
    .SET_TAIL(cell_20_set_tail), .IS_HEAD(cell_12_set_head), .IS_ACTIVE(cell_20_is_active),
    .IS_ACTIVE_LEFT(cell_12_is_active_2), .DATA_IN(cell_12_data_in_2), .DATA_OUT_2(cell_20_data_out_2),
    .CMD(cell_12_cmd_2), .CLK(cell_12_clk_2), .IS_TAIL(cell_28_set_tail), .SET_HEAD(cell_20_set_head),
    .IS_ACTIVE_RIGHT(cell_28_is_active), .IS_ACTIVE_2(cell_20_is_active_2), .DATA_IN_2(cell_20_data_in_2),
    .DATA_OUT(cell_28_data_out_2), .CMD_2(cell_20_cmd_2), .CLK_2(cell_20_clk_2),
    .DBG_MEM({cell_20_dbg_mem_2, cell_20_dbg_mem}),
    .DBG_LED({cell_20_dbg_led[2], DBGROW0_3[29], cell_20_dbg_led[0]}));
  Hex_Digit_Display hex_digit_display_44 (.value(cell_20_dbg_mem));  // open: dp
  \cell  cell_21 (
    .SET_TAIL(cell_21_set_tail), .IS_HEAD(cell_13_set_head), .IS_ACTIVE(cell_21_is_active),
    .IS_ACTIVE_LEFT(cell_13_is_active_2), .DATA_IN(cell_13_data_in_2), .DATA_OUT_2(cell_21_data_out_2),
    .CMD(cell_13_cmd_2), .CLK(cell_13_clk_2), .IS_TAIL(cell_29_set_tail), .SET_HEAD(cell_21_set_head),
    .IS_ACTIVE_RIGHT(cell_29_is_active), .IS_ACTIVE_2(cell_21_is_active_2), .DATA_IN_2(cell_21_data_in_2),
    .DATA_OUT(cell_29_data_out_2), .CMD_2(cell_21_cmd_2), .CLK_2(cell_21_clk_2),
    .DBG_MEM({cell_21_dbg_mem_2, cell_21_dbg_mem}),
    .DBG_LED({cell_21_dbg_led[2], DBGROW4_7[5], cell_21_dbg_led[0]}));
  Hex_Digit_Display hex_digit_display_45 (.value(cell_21_dbg_mem));  // open: dp
  \cell  cell_22 (
    .SET_TAIL(cell_22_set_tail), .IS_HEAD(cell_14_set_head), .IS_ACTIVE(cell_22_is_active),
    .IS_ACTIVE_LEFT(cell_14_is_active_2), .DATA_IN(cell_14_data_in_2), .DATA_OUT_2(cell_22_data_out_2),
    .CMD(cell_14_cmd_2), .CLK(cell_14_clk_2), .IS_TAIL(cell_30_set_tail), .SET_HEAD(cell_22_set_head),
    .IS_ACTIVE_RIGHT(cell_30_is_active), .IS_ACTIVE_2(cell_22_is_active_2), .DATA_IN_2(cell_22_data_in_2),
    .DATA_OUT(cell_30_data_out_2), .CMD_2(cell_22_cmd_2), .CLK_2(cell_22_clk_2),
    .DBG_MEM({cell_22_dbg_mem_2, cell_22_dbg_mem}),
    .DBG_LED({cell_22_dbg_led[2], DBGROW4_7[13], cell_22_dbg_led[0]}));
  Hex_Digit_Display hex_digit_display_46 (.value(cell_22_dbg_mem));  // open: dp
  \cell  cell_23 (
    .SET_TAIL(cell_23_set_tail), .IS_HEAD(cell_15_set_head), .IS_ACTIVE(cell_23_is_active),
    .IS_ACTIVE_LEFT(cell_15_is_active_2), .DATA_IN(cell_15_data_in_2), .DATA_OUT_2(cell_23_data_out_2),
    .CMD(cell_15_cmd_2), .CLK(cell_15_clk_2), .IS_TAIL(cell_31_set_tail), .SET_HEAD(cell_23_set_head),
    .IS_ACTIVE_RIGHT(cell_31_is_active), .IS_ACTIVE_2(cell_23_is_active_2), .DATA_IN_2(cell_23_data_in_2),
    .DATA_OUT(cell_31_data_out_2), .CMD_2(cell_23_cmd_2), .CLK_2(cell_23_clk_2), .DBG_MEM(cell_23_dbg_mem),
    .DBG_LED({cell_23_dbg_led[2], DBGROW4_7[21], cell_23_dbg_led[0]}));
  Hex_Digit_Display hex_digit_display_47 (.value(cell_23_dbg_mem[3:0]));  // open: dp
  \cell  cell_24 (
    .SET_TAIL(cell_24_set_tail), .IS_HEAD(cell_16_set_head), .IS_ACTIVE(cell_24_is_active),
    .IS_ACTIVE_LEFT(cell_16_is_active_2), .DATA_IN(cell_16_data_in_2), .DATA_OUT_2(cell_24_data_out_2),
    .CMD(cell_16_cmd_2), .CLK(cell_16_clk_2), .IS_TAIL(cell_32_set_tail), .SET_HEAD(cell_24_set_head),
    .IS_ACTIVE_RIGHT(cell_32_is_active), .IS_ACTIVE_2(cell_24_is_active_2), .DATA_IN_2(cell_24_data_in_2),
    .DATA_OUT(cell_32_data_out_2), .CMD_2(cell_24_cmd_2), .CLK_2(cell_24_clk_2), .DBG_MEM(cell_24_dbg_mem),
    .DBG_LED({cell_24_dbg_led[2], DBGROW4_7[29], cell_24_dbg_led[0]}));
  Hex_Digit_Display hex_digit_display_48 (.value(cell_24_dbg_mem[3:0]));  // open: dp
  \cell  cell_25 (
    .SET_TAIL(cell_25_set_tail), .IS_HEAD(cell_17_set_head), .IS_ACTIVE(cell_25_is_active),
    .IS_ACTIVE_LEFT(cell_17_is_active_2), .DATA_IN(cell_17_data_in_2), .DATA_OUT_2(cell_25_data_out_2),
    .CMD(cell_17_cmd_2), .CLK(cell_17_clk_2), .IS_TAIL(cell_33_set_tail), .SET_HEAD(cell_25_set_head),
    .IS_ACTIVE_RIGHT(cell_33_is_active), .IS_ACTIVE_2(cell_25_is_active_2), .DATA_IN_2(cell_25_data_in_2),
    .DATA_OUT(cell_33_data_out_2), .CMD_2(cell_25_cmd_2), .CLK_2(cell_25_clk_2),
    .DBG_MEM({cell_25_dbg_mem_2, cell_25_dbg_mem}),
    .DBG_LED({cell_25_dbg_led[2], DBGROW0_3[4], cell_25_dbg_led[0]}));
  Hex_Digit_Display hex_digit_display_49 (.value(cell_25_dbg_mem_2));  // open: dp
  Hex_Digit_Display hex_digit_display_50 (.value(cell_25_dbg_mem));  // open: dp
  \cell  cell_26 (
    .SET_TAIL(cell_26_set_tail), .IS_HEAD(cell_18_set_head), .IS_ACTIVE(cell_26_is_active),
    .IS_ACTIVE_LEFT(cell_18_is_active_2), .DATA_IN(cell_18_data_in_2), .DATA_OUT_2(cell_26_data_out_2),
    .CMD(cell_18_cmd_2), .CLK(cell_18_clk_2), .IS_TAIL(cell_34_set_tail), .SET_HEAD(cell_26_set_head),
    .IS_ACTIVE_RIGHT(cell_34_is_active), .IS_ACTIVE_2(cell_26_is_active_2), .DATA_IN_2(cell_26_data_in_2),
    .DATA_OUT(cell_34_data_out_2), .CMD_2(cell_26_cmd_2), .CLK_2(cell_26_clk_2), .DBG_MEM(cell_26_dbg_mem),
    .DBG_LED({cell_26_dbg_led[2], DBGROW0_3[12], cell_26_dbg_led[0]}));
  Hex_Digit_Display hex_digit_display_51 (.value(cell_26_dbg_mem[3:0]));  // open: dp
  Hex_Digit_Display hex_digit_display_52 (.value(cell_26_dbg_mem[7:4]));  // open: dp
  \cell  cell_27 (
    .SET_TAIL(cell_27_set_tail), .IS_HEAD(cell_19_set_head), .IS_ACTIVE(cell_27_is_active),
    .IS_ACTIVE_LEFT(cell_19_is_active_2), .DATA_IN(cell_19_data_in_2), .DATA_OUT_2(cell_27_data_out_2),
    .CMD(cell_19_cmd_2), .CLK(cell_19_clk_2), .IS_TAIL(cell_35_set_tail), .SET_HEAD(cell_27_set_head),
    .IS_ACTIVE_RIGHT(cell_35_is_active), .IS_ACTIVE_2(cell_27_is_active_2), .DATA_IN_2(cell_27_data_in_2),
    .DATA_OUT(cell_35_data_out_2), .CMD_2(cell_27_cmd_2), .CLK_2(cell_27_clk_2), .DBG_MEM(cell_27_dbg_mem),
    .DBG_LED({cell_27_dbg_led[2], DBGROW0_3[20], cell_27_dbg_led[0]}));
  Hex_Digit_Display hex_digit_display_53 (.value(cell_27_dbg_mem[7:4]));  // open: dp
  Hex_Digit_Display hex_digit_display_54 (.value(cell_27_dbg_mem[3:0]));  // open: dp
  \cell  cell_28 (
    .SET_TAIL(cell_28_set_tail), .IS_HEAD(cell_20_set_head), .IS_ACTIVE(cell_28_is_active),
    .IS_ACTIVE_LEFT(cell_20_is_active_2), .DATA_IN(cell_20_data_in_2), .DATA_OUT_2(cell_28_data_out_2),
    .CMD(cell_20_cmd_2), .CLK(cell_20_clk_2), .IS_TAIL(cell_36_set_tail), .SET_HEAD(cell_28_set_head),
    .IS_ACTIVE_RIGHT(cell_36_is_active), .IS_ACTIVE_2(cell_28_is_active_2), .DATA_IN_2(cell_28_data_in_2),
    .DATA_OUT(cell_36_data_out_2), .CMD_2(cell_28_cmd_2), .CLK_2(cell_28_clk_2), .DBG_MEM(cell_28_dbg_mem),
    .DBG_LED({cell_28_dbg_led[2], DBGROW0_3[28], cell_28_dbg_led[0]}));
  Hex_Digit_Display hex_digit_display_55 (.value(cell_28_dbg_mem[7:4]));  // open: dp
  Hex_Digit_Display hex_digit_display_56 (.value(cell_28_dbg_mem[3:0]));  // open: dp
  \cell  cell_29 (
    .SET_TAIL(cell_29_set_tail), .IS_HEAD(cell_21_set_head), .IS_ACTIVE(cell_29_is_active),
    .IS_ACTIVE_LEFT(cell_21_is_active_2), .DATA_IN(cell_21_data_in_2), .DATA_OUT_2(cell_29_data_out_2),
    .CMD(cell_21_cmd_2), .CLK(cell_21_clk_2), .IS_TAIL(cell_37_set_tail), .SET_HEAD(cell_29_set_head),
    .IS_ACTIVE_RIGHT(cell_37_is_active), .IS_ACTIVE_2(cell_29_is_active_2), .DATA_IN_2(cell_29_data_in_2),
    .DATA_OUT(cell_37_data_out_2), .CMD_2(cell_29_cmd_2), .CLK_2(cell_29_clk_2), .DBG_MEM(cell_29_dbg_mem),
    .DBG_LED({cell_29_dbg_led[2], DBGROW4_7[4], cell_29_dbg_led[0]}));
  Hex_Digit_Display hex_digit_display_57 (.value(cell_29_dbg_mem[7:4]));  // open: dp
  Hex_Digit_Display hex_digit_display_58 (.value(cell_29_dbg_mem[3:0]));  // open: dp
  \cell  cell_30 (
    .SET_TAIL(cell_30_set_tail), .IS_HEAD(cell_22_set_head), .IS_ACTIVE(cell_30_is_active),
    .IS_ACTIVE_LEFT(cell_22_is_active_2), .DATA_IN(cell_22_data_in_2), .DATA_OUT_2(cell_30_data_out_2),
    .CMD(cell_22_cmd_2), .CLK(cell_22_clk_2), .IS_TAIL(cell_38_set_tail), .SET_HEAD(cell_30_set_head),
    .IS_ACTIVE_RIGHT(cell_38_is_active), .IS_ACTIVE_2(cell_30_is_active_2), .DATA_IN_2(cell_30_data_in_2),
    .DATA_OUT(cell_38_data_out_2), .CMD_2(cell_30_cmd_2), .CLK_2(cell_30_clk_2), .DBG_MEM(cell_30_dbg_mem),
    .DBG_LED({cell_30_dbg_led[2], DBGROW4_7[12], cell_30_dbg_led[0]}));
  Hex_Digit_Display hex_digit_display_59 (.value(cell_30_dbg_mem[3:0]));  // open: dp
  Hex_Digit_Display hex_digit_display_60 (.value(cell_30_dbg_mem[7:4]));  // open: dp
  \cell  cell_31 (
    .SET_TAIL(cell_31_set_tail), .IS_HEAD(cell_23_set_head), .IS_ACTIVE(cell_31_is_active),
    .IS_ACTIVE_LEFT(cell_23_is_active_2), .DATA_IN(cell_23_data_in_2), .DATA_OUT_2(cell_31_data_out_2),
    .CMD(cell_23_cmd_2), .CLK(cell_23_clk_2), .IS_TAIL(cell_39_set_tail), .SET_HEAD(cell_31_set_head),
    .IS_ACTIVE_RIGHT(cell_39_is_active), .IS_ACTIVE_2(cell_31_is_active_2), .DATA_IN_2(cell_31_data_in_2),
    .DATA_OUT(cell_39_data_out_2), .CMD_2(cell_31_cmd_2), .CLK_2(cell_31_clk_2),
    .DBG_MEM({cell_31_dbg_mem_2, cell_31_dbg_mem}),
    .DBG_LED({cell_31_dbg_led[2], DBGROW4_7[20], cell_31_dbg_led[0]}));
  Hex_Digit_Display hex_digit_display_61 (.value(cell_31_dbg_mem));  // open: dp
  Hex_Digit_Display hex_digit_display_62 (.value(cell_31_dbg_mem_2));  // open: dp
  \cell  cell_32 (
    .SET_TAIL(cell_32_set_tail), .IS_HEAD(cell_24_set_head), .IS_ACTIVE(cell_32_is_active),
    .IS_ACTIVE_LEFT(cell_24_is_active_2), .DATA_IN(cell_24_data_in_2), .DATA_OUT_2(cell_32_data_out_2),
    .CMD(cell_24_cmd_2), .CLK(cell_24_clk_2), .IS_TAIL(cell_40_set_tail), .SET_HEAD(cell_32_set_head),
    .IS_ACTIVE_RIGHT(cell_40_is_active), .IS_ACTIVE_2(cell_32_is_active_2), .DATA_IN_2(cell_32_data_in_2),
    .DATA_OUT(cell_40_data_out_2), .CMD_2(cell_32_cmd_2), .CLK_2(cell_32_clk_2),
    .DBG_MEM({cell_32_dbg_mem_2, cell_32_dbg_mem}),
    .DBG_LED({cell_32_dbg_led[2], DBGROW4_7[28], cell_32_dbg_led[0]}));
  Hex_Digit_Display hex_digit_display_63 (.value(cell_32_dbg_mem));  // open: dp
  Hex_Digit_Display hex_digit_display_64 (.value(cell_32_dbg_mem_2));  // open: dp
  \cell  cell_33 (
    .SET_TAIL(cell_33_set_tail), .IS_HEAD(cell_25_set_head), .IS_ACTIVE(cell_33_is_active),
    .IS_ACTIVE_LEFT(cell_25_is_active_2), .DATA_IN(cell_25_data_in_2), .DATA_OUT_2(cell_33_data_out_2),
    .CMD(cell_25_cmd_2), .CLK(cell_25_clk_2), .IS_TAIL(cell_41_set_tail), .SET_HEAD(cell_33_set_head),
    .IS_ACTIVE_RIGHT(cell_41_is_active), .IS_ACTIVE_2(cell_33_is_active_2), .DATA_IN_2(cell_33_data_in_2),
    .DATA_OUT(cell_41_data_out_2), .CMD_2(cell_33_cmd_2), .CLK_2(cell_33_clk_2),
    .DBG_MEM({cell_33_dbg_mem_2, cell_33_dbg_mem}),
    .DBG_LED({cell_33_dbg_led[2], DBGROW0_3[3], cell_33_dbg_led[0]}));
  Hex_Digit_Display hex_digit_display_65 (.value(cell_33_dbg_mem_2));  // open: dp
  \cell  cell_34 (
    .SET_TAIL(cell_34_set_tail), .IS_HEAD(cell_26_set_head), .IS_ACTIVE(cell_34_is_active),
    .IS_ACTIVE_LEFT(cell_26_is_active_2), .DATA_IN(cell_26_data_in_2), .DATA_OUT_2(cell_34_data_out_2),
    .CMD(cell_26_cmd_2), .CLK(cell_26_clk_2), .IS_TAIL(cell_42_set_tail), .SET_HEAD(cell_34_set_head),
    .IS_ACTIVE_RIGHT(cell_42_is_active), .IS_ACTIVE_2(cell_34_is_active_2), .DATA_IN_2(cell_34_data_in_2),
    .DATA_OUT(cell_42_data_out_2), .CMD_2(cell_34_cmd_2), .CLK_2(cell_34_clk_2),
    .DBG_MEM({cell_34_dbg_mem_2, cell_34_dbg_mem}),
    .DBG_LED({cell_34_dbg_led[2], DBGROW0_3[11], cell_34_dbg_led[0]}));
  Hex_Digit_Display hex_digit_display_66 (.value(cell_34_dbg_mem_2));  // open: dp
  \cell  cell_35 (
    .SET_TAIL(cell_35_set_tail), .IS_HEAD(cell_27_set_head), .IS_ACTIVE(cell_35_is_active),
    .IS_ACTIVE_LEFT(cell_27_is_active_2), .DATA_IN(cell_27_data_in_2), .DATA_OUT_2(cell_35_data_out_2),
    .CMD(cell_27_cmd_2), .CLK(cell_27_clk_2), .IS_TAIL(cell_43_set_tail), .SET_HEAD(cell_35_set_head),
    .IS_ACTIVE_RIGHT(cell_43_is_active), .IS_ACTIVE_2(cell_35_is_active_2), .DATA_IN_2(cell_35_data_in_2),
    .DATA_OUT(cell_43_data_out_2), .CMD_2(cell_35_cmd_2), .CLK_2(cell_35_clk_2),
    .DBG_MEM({cell_35_dbg_mem_2, cell_35_dbg_mem}),
    .DBG_LED({cell_35_dbg_led[2], DBGROW0_3[19], cell_35_dbg_led[0]}));
  Hex_Digit_Display hex_digit_display_67 (.value(cell_35_dbg_mem_2));  // open: dp
  \cell  cell_36 (
    .SET_TAIL(cell_36_set_tail), .IS_HEAD(cell_28_set_head), .IS_ACTIVE(cell_36_is_active),
    .IS_ACTIVE_LEFT(cell_28_is_active_2), .DATA_IN(cell_28_data_in_2), .DATA_OUT_2(cell_36_data_out_2),
    .CMD(cell_28_cmd_2), .CLK(cell_28_clk_2), .IS_TAIL(cell_44_set_tail), .SET_HEAD(cell_36_set_head),
    .IS_ACTIVE_RIGHT(cell_44_is_active), .IS_ACTIVE_2(cell_36_is_active_2), .DATA_IN_2(cell_36_data_in_2),
    .DATA_OUT(cell_44_data_out_2), .CMD_2(cell_36_cmd_2), .CLK_2(cell_36_clk_2), .DBG_MEM(cell_36_dbg_mem),
    .DBG_LED({cell_36_dbg_led[2], DBGROW0_3[27], cell_36_dbg_led[0]}));
  Hex_Digit_Display hex_digit_display_68 (.value(cell_36_dbg_mem[7:4]));  // open: dp
  \cell  cell_37 (
    .SET_TAIL(cell_37_set_tail), .IS_HEAD(cell_29_set_head), .IS_ACTIVE(cell_37_is_active),
    .IS_ACTIVE_LEFT(cell_29_is_active_2), .DATA_IN(cell_29_data_in_2), .DATA_OUT_2(cell_37_data_out_2),
    .CMD(cell_29_cmd_2), .CLK(cell_29_clk_2), .IS_TAIL(cell_45_set_tail), .SET_HEAD(cell_37_set_head),
    .IS_ACTIVE_RIGHT(cell_45_is_active), .IS_ACTIVE_2(cell_37_is_active_2), .DATA_IN_2(cell_37_data_in_2),
    .DATA_OUT(cell_45_data_out_2), .CMD_2(cell_37_cmd_2), .CLK_2(cell_37_clk_2), .DBG_MEM(cell_37_dbg_mem),
    .DBG_LED({cell_37_dbg_led[2], DBGROW4_7[3], cell_37_dbg_led[0]}));
  Hex_Digit_Display hex_digit_display_69 (.value(cell_37_dbg_mem[7:4]));  // open: dp
  \cell  cell_38 (
    .SET_TAIL(cell_38_set_tail), .IS_HEAD(cell_30_set_head), .IS_ACTIVE(cell_38_is_active),
    .IS_ACTIVE_LEFT(cell_30_is_active_2), .DATA_IN(cell_30_data_in_2), .DATA_OUT_2(cell_38_data_out_2),
    .CMD(cell_30_cmd_2), .CLK(cell_30_clk_2), .IS_TAIL(cell_46_set_tail), .SET_HEAD(cell_38_set_head),
    .IS_ACTIVE_RIGHT(cell_46_is_active), .IS_ACTIVE_2(cell_38_is_active_2), .DATA_IN_2(cell_38_data_in_2),
    .DATA_OUT(cell_46_data_out_2), .CMD_2(cell_38_cmd_2), .CLK_2(cell_38_clk_2), .DBG_MEM(cell_38_dbg_mem),
    .DBG_LED({cell_38_dbg_led[2], DBGROW4_7[11], cell_38_dbg_led[0]}));
  Hex_Digit_Display hex_digit_display_70 (.value(cell_38_dbg_mem[7:4]));  // open: dp
  \cell  cell_39 (
    .SET_TAIL(cell_39_set_tail), .IS_HEAD(cell_31_set_head), .IS_ACTIVE(cell_39_is_active),
    .IS_ACTIVE_LEFT(cell_31_is_active_2), .DATA_IN(cell_31_data_in_2), .DATA_OUT_2(cell_39_data_out_2),
    .CMD(cell_31_cmd_2), .CLK(cell_31_clk_2), .IS_TAIL(cell_47_set_tail), .SET_HEAD(cell_39_set_head),
    .IS_ACTIVE_RIGHT(cell_47_is_active), .IS_ACTIVE_2(cell_39_is_active_2), .DATA_IN_2(cell_39_data_in_2),
    .DATA_OUT(cell_47_data_out_2), .CMD_2(cell_39_cmd_2), .CLK_2(cell_39_clk_2), .DBG_MEM(cell_39_dbg_mem),
    .DBG_LED({cell_39_dbg_led[2], DBGROW4_7[19], cell_39_dbg_led[0]}));
  Hex_Digit_Display hex_digit_display_71 (.value(cell_39_dbg_mem[7:4]));  // open: dp
  \cell  cell_40 (
    .SET_TAIL(cell_40_set_tail), .IS_HEAD(cell_32_set_head), .IS_ACTIVE(cell_40_is_active),
    .IS_ACTIVE_LEFT(cell_32_is_active_2), .DATA_IN(cell_32_data_in_2), .DATA_OUT_2(cell_40_data_out_2),
    .CMD(cell_32_cmd_2), .CLK(cell_32_clk_2), .IS_TAIL(cell_48_set_tail), .SET_HEAD(cell_40_set_head),
    .IS_ACTIVE_RIGHT(cell_48_is_active), .IS_ACTIVE_2(cell_40_is_active_2), .DATA_IN_2(cell_40_data_in_2),
    .DATA_OUT(cell_48_data_out_2), .CMD_2(cell_40_cmd_2), .CLK_2(cell_40_clk_2), .DBG_MEM(cell_40_dbg_mem),
    .DBG_LED({cell_40_dbg_led[2], DBGROW4_7[27], cell_40_dbg_led[0]}));
  Hex_Digit_Display hex_digit_display_72 (.value(cell_40_dbg_mem[7:4]));  // open: dp
  Hex_Digit_Display hex_digit_display_73 (.value(cell_41_dbg_mem[7:4]));  // open: dp
  Hex_Digit_Display hex_digit_display_74 (.value(cell_33_dbg_mem));  // open: dp
  Hex_Digit_Display hex_digit_display_75 (.value(cell_34_dbg_mem));  // open: dp
  Hex_Digit_Display hex_digit_display_76 (.value(cell_42_dbg_mem[7:4]));  // open: dp
  Hex_Digit_Display hex_digit_display_77 (.value(cell_43_dbg_mem_2));  // open: dp
  Hex_Digit_Display hex_digit_display_78 (.value(cell_35_dbg_mem));  // open: dp
  Hex_Digit_Display hex_digit_display_79 (.value(cell_36_dbg_mem[3:0]));  // open: dp
  Hex_Digit_Display hex_digit_display_80 (.value(cell_44_dbg_mem_2));  // open: dp
  Hex_Digit_Display hex_digit_display_81 (.value(cell_37_dbg_mem[3:0]));  // open: dp
  Hex_Digit_Display hex_digit_display_82 (.value(cell_45_dbg_mem_2));  // open: dp
  Hex_Digit_Display hex_digit_display_83 (.value(cell_46_dbg_mem[7:4]));  // open: dp
  Hex_Digit_Display hex_digit_display_84 (.value(cell_38_dbg_mem[3:0]));  // open: dp
  Hex_Digit_Display hex_digit_display_85 (.value(cell_47_dbg_mem[7:4]));  // open: dp
  Hex_Digit_Display hex_digit_display_86 (.value(cell_39_dbg_mem[3:0]));  // open: dp
  Hex_Digit_Display hex_digit_display_87 (.value(cell_40_dbg_mem[3:0]));  // open: dp
  Hex_Digit_Display hex_digit_display_88 (.value(cell_48_dbg_mem[7:4]));  // open: dp
  \cell  cell_41 (
    .SET_TAIL(cell_41_set_tail), .IS_HEAD(cell_33_set_head), .IS_ACTIVE(cell_41_is_active),
    .IS_ACTIVE_LEFT(cell_33_is_active_2), .DATA_IN(cell_33_data_in_2), .DATA_OUT_2(cell_41_data_out_2),
    .CMD(cell_33_cmd_2), .CLK(cell_33_clk_2), .IS_TAIL(cell_49_set_tail), .SET_HEAD(cell_41_set_head),
    .IS_ACTIVE_RIGHT(cell_49_is_active), .IS_ACTIVE_2(cell_41_is_active_2), .DATA_IN_2(cell_41_data_in_2),
    .DATA_OUT(cell_49_data_out_2), .CMD_2(cell_41_cmd_2), .CLK_2(cell_41_clk_2), .DBG_MEM(cell_41_dbg_mem),
    .DBG_LED({cell_41_dbg_led[2], DBGROW0_3[2], cell_41_dbg_led[0]}));
  Hex_Digit_Display hex_digit_display_89 (.value(cell_41_dbg_mem[3:0]));  // open: dp
  \cell  cell_42 (
    .SET_TAIL(cell_42_set_tail), .IS_HEAD(cell_34_set_head), .IS_ACTIVE(cell_42_is_active),
    .IS_ACTIVE_LEFT(cell_34_is_active_2), .DATA_IN(cell_34_data_in_2), .DATA_OUT_2(cell_42_data_out_2),
    .CMD(cell_34_cmd_2), .CLK(cell_34_clk_2), .IS_TAIL(cell_50_set_tail), .SET_HEAD(cell_42_set_head),
    .IS_ACTIVE_RIGHT(cell_50_is_active), .IS_ACTIVE_2(cell_42_is_active_2), .DATA_IN_2(cell_42_data_in_2),
    .DATA_OUT(cell_50_data_out_2), .CMD_2(cell_42_cmd_2), .CLK_2(cell_42_clk_2), .DBG_MEM(cell_42_dbg_mem),
    .DBG_LED({cell_42_dbg_led[2], DBGROW0_3[10], cell_42_dbg_led[0]}));
  Hex_Digit_Display hex_digit_display_90 (.value(cell_42_dbg_mem[3:0]));  // open: dp
  \cell  cell_43 (
    .SET_TAIL(cell_43_set_tail), .IS_HEAD(cell_35_set_head), .IS_ACTIVE(cell_43_is_active),
    .IS_ACTIVE_LEFT(cell_35_is_active_2), .DATA_IN(cell_35_data_in_2), .DATA_OUT_2(cell_43_data_out_2),
    .CMD(cell_35_cmd_2), .CLK(cell_35_clk_2), .IS_TAIL(cell_51_set_tail), .SET_HEAD(cell_43_set_head),
    .IS_ACTIVE_RIGHT(cell_51_is_active), .IS_ACTIVE_2(cell_43_is_active_2), .DATA_IN_2(cell_43_data_in_2),
    .DATA_OUT(cell_51_data_out_2), .CMD_2(cell_43_cmd_2), .CLK_2(cell_43_clk_2),
    .DBG_MEM({cell_43_dbg_mem_2, cell_43_dbg_mem}),
    .DBG_LED({cell_43_dbg_led[2], DBGROW0_3[18], cell_43_dbg_led[0]}));
  Hex_Digit_Display hex_digit_display_91 (.value(cell_43_dbg_mem));  // open: dp
  \cell  cell_44 (
    .SET_TAIL(cell_44_set_tail), .IS_HEAD(cell_36_set_head), .IS_ACTIVE(cell_44_is_active),
    .IS_ACTIVE_LEFT(cell_36_is_active_2), .DATA_IN(cell_36_data_in_2), .DATA_OUT_2(cell_44_data_out_2),
    .CMD(cell_36_cmd_2), .CLK(cell_36_clk_2), .IS_TAIL(cell_52_set_tail), .SET_HEAD(cell_44_set_head),
    .IS_ACTIVE_RIGHT(cell_52_is_active), .IS_ACTIVE_2(cell_44_is_active_2), .DATA_IN_2(cell_44_data_in_2),
    .DATA_OUT(cell_52_data_out_2), .CMD_2(cell_44_cmd_2), .CLK_2(cell_44_clk_2),
    .DBG_MEM({cell_44_dbg_mem_2, cell_44_dbg_mem}),
    .DBG_LED({cell_44_dbg_led[2], DBGROW0_3[26], cell_44_dbg_led[0]}));
  Hex_Digit_Display hex_digit_display_92 (.value(cell_44_dbg_mem));  // open: dp
  \cell  cell_45 (
    .SET_TAIL(cell_45_set_tail), .IS_HEAD(cell_37_set_head), .IS_ACTIVE(cell_45_is_active),
    .IS_ACTIVE_LEFT(cell_37_is_active_2), .DATA_IN(cell_37_data_in_2), .DATA_OUT_2(cell_45_data_out_2),
    .CMD(cell_37_cmd_2), .CLK(cell_37_clk_2), .IS_TAIL(cell_53_set_tail), .SET_HEAD(cell_45_set_head),
    .IS_ACTIVE_RIGHT(cell_53_is_active), .IS_ACTIVE_2(cell_45_is_active_2), .DATA_IN_2(cell_45_data_in_2),
    .DATA_OUT(cell_53_data_out_2), .CMD_2(cell_45_cmd_2), .CLK_2(cell_45_clk_2),
    .DBG_MEM({cell_45_dbg_mem_2, cell_45_dbg_mem}),
    .DBG_LED({cell_45_dbg_led[2], DBGROW4_7[2], cell_45_dbg_led[0]}));
  Hex_Digit_Display hex_digit_display_93 (.value(cell_45_dbg_mem));  // open: dp
  \cell  cell_46 (
    .SET_TAIL(cell_46_set_tail), .IS_HEAD(cell_38_set_head), .IS_ACTIVE(cell_46_is_active),
    .IS_ACTIVE_LEFT(cell_38_is_active_2), .DATA_IN(cell_38_data_in_2), .DATA_OUT_2(cell_46_data_out_2),
    .CMD(cell_38_cmd_2), .CLK(cell_38_clk_2), .IS_TAIL(cell_54_set_tail), .SET_HEAD(cell_46_set_head),
    .IS_ACTIVE_RIGHT(cell_54_is_active), .IS_ACTIVE_2(cell_46_is_active_2), .DATA_IN_2(cell_46_data_in_2),
    .DATA_OUT(cell_54_data_out_2), .CMD_2(cell_46_cmd_2), .CLK_2(cell_46_clk_2), .DBG_MEM(cell_46_dbg_mem),
    .DBG_LED({cell_46_dbg_led[2], DBGROW4_7[10], cell_46_dbg_led[0]}));
  Hex_Digit_Display hex_digit_display_94 (.value(cell_46_dbg_mem[3:0]));  // open: dp
  \cell  cell_47 (
    .SET_TAIL(cell_47_set_tail), .IS_HEAD(cell_39_set_head), .IS_ACTIVE(cell_47_is_active),
    .IS_ACTIVE_LEFT(cell_39_is_active_2), .DATA_IN(cell_39_data_in_2), .DATA_OUT_2(cell_47_data_out_2),
    .CMD(cell_39_cmd_2), .CLK(cell_39_clk_2), .IS_TAIL(cell_55_set_tail), .SET_HEAD(cell_47_set_head),
    .IS_ACTIVE_RIGHT(cell_55_is_active), .IS_ACTIVE_2(cell_47_is_active_2), .DATA_IN_2(cell_47_data_in_2),
    .DATA_OUT(cell_55_data_out_2), .CMD_2(cell_47_cmd_2), .CLK_2(cell_47_clk_2), .DBG_MEM(cell_47_dbg_mem),
    .DBG_LED({cell_47_dbg_led[2], DBGROW4_7[18], cell_47_dbg_led[0]}));
  Hex_Digit_Display hex_digit_display_95 (.value(cell_47_dbg_mem[3:0]));  // open: dp
  \cell  cell_48 (
    .SET_TAIL(cell_48_set_tail), .IS_HEAD(cell_40_set_head), .IS_ACTIVE(cell_48_is_active),
    .IS_ACTIVE_LEFT(cell_40_is_active_2), .DATA_IN(cell_40_data_in_2), .DATA_OUT_2(cell_48_data_out_2),
    .CMD(cell_40_cmd_2), .CLK(cell_40_clk_2), .IS_TAIL(cell_56_set_tail), .SET_HEAD(cell_48_set_head),
    .IS_ACTIVE_RIGHT(cell_56_is_active), .IS_ACTIVE_2(cell_48_is_active_2), .DATA_IN_2(cell_48_data_in_2),
    .DATA_OUT(cell_56_data_out_2), .CMD_2(cell_48_cmd_2), .CLK_2(cell_48_clk_2), .DBG_MEM(cell_48_dbg_mem),
    .DBG_LED({cell_48_dbg_led[2], DBGROW4_7[26], cell_48_dbg_led[0]}));
  Hex_Digit_Display hex_digit_display_96 (.value(cell_48_dbg_mem[3:0]));  // open: dp
  \cell  cell_49 (
    .SET_TAIL(cell_49_set_tail), .IS_HEAD(cell_41_set_head), .IS_ACTIVE(cell_49_is_active),
    .IS_ACTIVE_LEFT(cell_41_is_active_2), .DATA_IN(cell_41_data_in_2), .DATA_OUT_2(cell_49_data_out_2),
    .CMD(cell_41_cmd_2), .CLK(cell_41_clk_2), .IS_TAIL(cell_57_set_tail), .SET_HEAD(cell_49_set_head),
    .IS_ACTIVE_RIGHT(cell_57_is_active), .IS_ACTIVE_2(cell_49_is_active_2), .DATA_IN_2(cell_49_data_in_2),
    .DATA_OUT(cell_57_data_out_2), .CMD_2(cell_49_cmd_2), .CLK_2(cell_49_clk_2), .DBG_MEM(cell_49_dbg_mem),
    .DBG_LED({cell_49_dbg_led[2], DBGROW0_3[1], cell_49_dbg_led[0]}));
  Hex_Digit_Display hex_digit_display_97 (.value(cell_49_dbg_mem[3:0]));  // open: dp
  Hex_Digit_Display hex_digit_display_98 (.value(cell_49_dbg_mem[7:4]));  // open: dp
  \cell  cell_50 (
    .SET_TAIL(cell_50_set_tail), .IS_HEAD(cell_42_set_head), .IS_ACTIVE(cell_50_is_active),
    .IS_ACTIVE_LEFT(cell_42_is_active_2), .DATA_IN(cell_42_data_in_2), .DATA_OUT_2(cell_50_data_out_2),
    .CMD(cell_42_cmd_2), .CLK(cell_42_clk_2), .IS_TAIL(cell_58_set_tail), .SET_HEAD(cell_50_set_head),
    .IS_ACTIVE_RIGHT(cell_58_is_active), .IS_ACTIVE_2(cell_50_is_active_2), .DATA_IN_2(cell_50_data_in_2),
    .DATA_OUT(cell_58_data_out_2), .CMD_2(cell_50_cmd_2), .CLK_2(cell_50_clk_2), .DBG_MEM(cell_50_dbg_mem),
    .DBG_LED({cell_50_dbg_led[2], DBGROW0_3[9], cell_50_dbg_led[0]}));
  Hex_Digit_Display hex_digit_display_99 (.value(cell_50_dbg_mem[7:4]));  // open: dp
  Hex_Digit_Display hex_digit_display_100 (.value(cell_50_dbg_mem[3:0]));  // open: dp
  \cell  cell_51 (
    .SET_TAIL(cell_51_set_tail), .IS_HEAD(cell_43_set_head), .IS_ACTIVE(cell_51_is_active),
    .IS_ACTIVE_LEFT(cell_43_is_active_2), .DATA_IN(cell_43_data_in_2), .DATA_OUT_2(cell_51_data_out_2),
    .CMD(cell_43_cmd_2), .CLK(cell_43_clk_2), .IS_TAIL(cell_59_set_tail), .SET_HEAD(cell_51_set_head),
    .IS_ACTIVE_RIGHT(cell_59_is_active), .IS_ACTIVE_2(cell_51_is_active_2), .DATA_IN_2(cell_51_data_in_2),
    .DATA_OUT(cell_59_data_out_2), .CMD_2(cell_51_cmd_2), .CLK_2(cell_51_clk_2), .DBG_MEM(cell_51_dbg_mem),
    .DBG_LED({cell_51_dbg_led[2], DBGROW0_3[17], cell_51_dbg_led[0]}));
  Hex_Digit_Display hex_digit_display_101 (.value(cell_51_dbg_mem[3:0]));  // open: dp
  Hex_Digit_Display hex_digit_display_102 (.value(cell_51_dbg_mem[7:4]));  // open: dp
  \cell  cell_52 (
    .SET_TAIL(cell_52_set_tail), .IS_HEAD(cell_44_set_head), .IS_ACTIVE(cell_52_is_active),
    .IS_ACTIVE_LEFT(cell_44_is_active_2), .DATA_IN(cell_44_data_in_2), .DATA_OUT_2(cell_52_data_out_2),
    .CMD(cell_44_cmd_2), .CLK(cell_44_clk_2), .IS_TAIL(cell_60_set_tail), .SET_HEAD(cell_52_set_head),
    .IS_ACTIVE_RIGHT(cell_60_is_active), .IS_ACTIVE_2(cell_52_is_active_2), .DATA_IN_2(cell_52_data_in_2),
    .DATA_OUT(cell_60_data_out_2), .CMD_2(cell_52_cmd_2), .CLK_2(cell_52_clk_2), .DBG_MEM(cell_52_dbg_mem),
    .DBG_LED({cell_52_dbg_led[2], DBGROW0_3[25], cell_52_dbg_led[0]}));
  Hex_Digit_Display hex_digit_display_103 (.value(cell_52_dbg_mem[3:0]));  // open: dp
  Hex_Digit_Display hex_digit_display_104 (.value(cell_52_dbg_mem[7:4]));  // open: dp
  \cell  cell_53 (
    .SET_TAIL(cell_53_set_tail), .IS_HEAD(cell_45_set_head), .IS_ACTIVE(cell_53_is_active),
    .IS_ACTIVE_LEFT(cell_45_is_active_2), .DATA_IN(cell_45_data_in_2), .DATA_OUT_2(cell_53_data_out_2),
    .CMD(cell_45_cmd_2), .CLK(cell_45_clk_2), .IS_TAIL(cell_61_set_tail), .SET_HEAD(cell_53_set_head),
    .IS_ACTIVE_RIGHT(cell_61_is_active), .IS_ACTIVE_2(cell_53_is_active_2), .DATA_IN_2(cell_53_data_in_2),
    .DATA_OUT(cell_61_data_out_2), .CMD_2(cell_53_cmd_2), .CLK_2(cell_53_clk_2),
    .DBG_MEM({cell_53_dbg_mem_2, cell_53_dbg_mem}),
    .DBG_LED({cell_53_dbg_led[2], DBGROW4_7[1], cell_53_dbg_led[0]}));
  Hex_Digit_Display hex_digit_display_105 (.value(cell_53_dbg_mem));  // open: dp
  Hex_Digit_Display hex_digit_display_106 (.value(cell_53_dbg_mem_2));  // open: dp
  \cell  cell_54 (
    .SET_TAIL(cell_54_set_tail), .IS_HEAD(cell_46_set_head), .IS_ACTIVE(cell_54_is_active),
    .IS_ACTIVE_LEFT(cell_46_is_active_2), .DATA_IN(cell_46_data_in_2), .DATA_OUT_2(cell_54_data_out_2),
    .CMD(cell_46_cmd_2), .CLK(cell_46_clk_2), .IS_TAIL(cell_62_set_tail), .SET_HEAD(cell_54_set_head),
    .IS_ACTIVE_RIGHT(cell_62_is_active), .IS_ACTIVE_2(cell_54_is_active_2), .DATA_IN_2(cell_54_data_in_2),
    .DATA_OUT(cell_62_data_out_2), .CMD_2(cell_54_cmd_2), .CLK_2(cell_54_clk_2),
    .DBG_MEM({cell_54_dbg_mem_2, cell_54_dbg_mem}),
    .DBG_LED({cell_54_dbg_led[2], DBGROW4_7[9], cell_54_dbg_led[0]}));
  Hex_Digit_Display hex_digit_display_107 (.value(cell_54_dbg_mem_2));  // open: dp
  Hex_Digit_Display hex_digit_display_108 (.value(cell_54_dbg_mem));  // open: dp
  \cell  cell_55 (
    .SET_TAIL(cell_55_set_tail), .IS_HEAD(cell_47_set_head), .IS_ACTIVE(cell_55_is_active),
    .IS_ACTIVE_LEFT(cell_47_is_active_2), .DATA_IN(cell_47_data_in_2), .DATA_OUT_2(cell_55_data_out_2),
    .CMD(cell_47_cmd_2), .CLK(cell_47_clk_2), .IS_TAIL(cell_63_set_tail), .SET_HEAD(cell_55_set_head),
    .IS_ACTIVE_RIGHT(cell_63_is_active), .IS_ACTIVE_2(cell_55_is_active_2), .DATA_IN_2(cell_55_data_in_2),
    .DATA_OUT(cell_63_data_out_2), .CMD_2(cell_55_cmd_2), .CLK_2(cell_55_clk_2),
    .DBG_MEM({cell_55_dbg_mem_2, cell_55_dbg_mem}),
    .DBG_LED({cell_55_dbg_led[2], DBGROW4_7[17], cell_55_dbg_led[0]}));
  Hex_Digit_Display hex_digit_display_109 (.value(cell_55_dbg_mem_2));  // open: dp
  Hex_Digit_Display hex_digit_display_110 (.value(cell_55_dbg_mem));  // open: dp
  \cell  cell_56 (
    .SET_TAIL(cell_56_set_tail), .IS_HEAD(cell_48_set_head), .IS_ACTIVE(cell_56_is_active),
    .IS_ACTIVE_LEFT(cell_48_is_active_2), .DATA_IN(cell_48_data_in_2), .DATA_OUT_2(cell_56_data_out_2),
    .CMD(cell_48_cmd_2), .CLK(cell_48_clk_2), .IS_TAIL(cell_64_set_tail), .SET_HEAD(cell_56_set_head),
    .IS_ACTIVE_RIGHT(cell_64_is_active), .IS_ACTIVE_2(cell_56_is_active_2), .DATA_IN_2(cell_56_data_in_2),
    .DATA_OUT(cell_64_data_out_2), .CMD_2(cell_56_cmd_2), .CLK_2(cell_56_clk_2), .DBG_MEM(cell_56_dbg_mem),
    .DBG_LED({cell_56_dbg_led[2], DBGROW4_7[25], cell_56_dbg_led[0]}));
  Hex_Digit_Display hex_digit_display_111 (.value(cell_56_dbg_mem[3:0]));  // open: dp
  Hex_Digit_Display hex_digit_display_112 (.value(cell_56_dbg_mem[7:4]));  // open: dp
  Hex_Digit_Display hex_digit_display_113 (.value(cell_57_dbg_mem_2));  // open: dp
  Hex_Digit_Display hex_digit_display_114 (.value(cell_58_dbg_mem_2));  // open: dp
  Hex_Digit_Display hex_digit_display_115 (.value(cell_59_dbg_mem_2));  // open: dp
  Hex_Digit_Display hex_digit_display_116 (.value(cell_60_dbg_mem_2));  // open: dp
  Hex_Digit_Display hex_digit_display_117 (.value(cell_61_dbg_mem_2));  // open: dp
  Hex_Digit_Display hex_digit_display_118 (.value(cell_62_dbg_mem_2));  // open: dp
  Hex_Digit_Display hex_digit_display_119 (.value(cell_63_dbg_mem_2));  // open: dp
  Hex_Digit_Display hex_digit_display_120 (.value(cell_64_dbg_mem_2));  // open: dp
  \cell  cell_57 (
    .SET_TAIL(cell_57_set_tail), .IS_HEAD(cell_49_set_head), .IS_ACTIVE(cell_57_is_active),
    .IS_ACTIVE_LEFT(cell_49_is_active_2), .DATA_IN(cell_49_data_in_2), .DATA_OUT_2(cell_57_data_out_2),
    .CMD(cell_49_cmd_2), .CLK(cell_49_clk_2), .IS_TAIL(ROW0_ROW1[0]), .SET_HEAD(ROW0_ROW1[1]),
    .IS_ACTIVE_RIGHT(ROW0_ROW1[2]), .IS_ACTIVE_2(ROW0_ROW1[3]), .DATA_IN_2(ROW0_ROW1[11:4]),
    .DATA_OUT(ROW0_ROW1[19:12]), .CMD_2(ROW0_ROW1[22:20]), .CLK_2(ROW0_ROW1[23]),
    .DBG_MEM({cell_57_dbg_mem_2, cell_57_dbg_mem}),
    .DBG_LED({cell_57_dbg_led[2], DBGROW0_3[0], cell_57_dbg_led[0]}));
  Hex_Digit_Display hex_digit_display_121 (.value(cell_57_dbg_mem));  // open: dp
  \cell  cell_58 (
    .SET_TAIL(cell_58_set_tail), .IS_HEAD(cell_50_set_head), .IS_ACTIVE(cell_58_is_active),
    .IS_ACTIVE_LEFT(cell_50_is_active_2), .DATA_IN(cell_50_data_in_2), .DATA_OUT_2(cell_58_data_out_2),
    .CMD(cell_50_cmd_2), .CLK(cell_50_clk_2), .IS_TAIL(ROW1_ROW2[0]), .SET_HEAD(ROW1_ROW2[1]),
    .IS_ACTIVE_RIGHT(ROW1_ROW2[2]), .IS_ACTIVE_2(ROW1_ROW2[3]), .DATA_IN_2(ROW1_ROW2[11:4]),
    .DATA_OUT(ROW1_ROW2[19:12]), .CMD_2(ROW1_ROW2[22:20]), .CLK_2(ROW1_ROW2[23]),
    .DBG_MEM({cell_58_dbg_mem_2, cell_58_dbg_mem}),
    .DBG_LED({cell_58_dbg_led[2], DBGROW0_3[8], cell_58_dbg_led[0]}));
  Hex_Digit_Display hex_digit_display_122 (.value(cell_58_dbg_mem));  // open: dp
  \cell  cell_59 (
    .SET_TAIL(cell_59_set_tail), .IS_HEAD(cell_51_set_head), .IS_ACTIVE(cell_59_is_active),
    .IS_ACTIVE_LEFT(cell_51_is_active_2), .DATA_IN(cell_51_data_in_2), .DATA_OUT_2(cell_59_data_out_2),
    .CMD(cell_51_cmd_2), .CLK(cell_51_clk_2), .IS_TAIL(ROW2_ROW3[0]), .SET_HEAD(ROW2_ROW3[1]),
    .IS_ACTIVE_RIGHT(ROW2_ROW3[2]), .IS_ACTIVE_2(ROW2_ROW3[3]), .DATA_IN_2(ROW2_ROW3[11:4]),
    .DATA_OUT(ROW2_ROW3[19:12]), .CMD_2(ROW2_ROW3[22:20]), .CLK_2(ROW2_ROW3[23]),
    .DBG_MEM({cell_59_dbg_mem_2, cell_59_dbg_mem}),
    .DBG_LED({cell_59_dbg_led[2], DBGROW0_3[16], cell_59_dbg_led[0]}));
  Hex_Digit_Display hex_digit_display_123 (.value(cell_59_dbg_mem));  // open: dp
  \cell  cell_60 (
    .SET_TAIL(cell_60_set_tail), .IS_HEAD(cell_52_set_head), .IS_ACTIVE(cell_60_is_active),
    .IS_ACTIVE_LEFT(cell_52_is_active_2), .DATA_IN(cell_52_data_in_2), .DATA_OUT_2(cell_60_data_out_2),
    .CMD(cell_52_cmd_2), .CLK(cell_52_clk_2), .IS_TAIL(ROW3_ROW4[0]), .SET_HEAD(ROW3_ROW4[1]),
    .IS_ACTIVE_RIGHT(ROW3_ROW4[2]), .IS_ACTIVE_2(ROW3_ROW4[3]), .DATA_IN_2(ROW3_ROW4[11:4]),
    .DATA_OUT(ROW3_ROW4[19:12]), .CMD_2(ROW3_ROW4[22:20]), .CLK_2(ROW3_ROW4[23]),
    .DBG_MEM({cell_60_dbg_mem_2, cell_60_dbg_mem}),
    .DBG_LED({cell_60_dbg_led[2], DBGROW0_3[24], cell_60_dbg_led[0]}));
  Hex_Digit_Display hex_digit_display_124 (.value(cell_60_dbg_mem));  // open: dp
  \cell  cell_61 (
    .SET_TAIL(cell_61_set_tail), .IS_HEAD(cell_53_set_head), .IS_ACTIVE(cell_61_is_active),
    .IS_ACTIVE_LEFT(cell_53_is_active_2), .DATA_IN(cell_53_data_in_2), .DATA_OUT_2(cell_61_data_out_2),
    .CMD(cell_53_cmd_2), .CLK(cell_53_clk_2), .IS_TAIL(ROW4_ROW5[0]), .SET_HEAD(ROW4_ROW5[1]),
    .IS_ACTIVE_RIGHT(ROW4_ROW5[2]), .IS_ACTIVE_2(ROW4_ROW5[3]), .DATA_IN_2(ROW4_ROW5[11:4]),
    .DATA_OUT(ROW4_ROW5[19:12]), .CMD_2(ROW4_ROW5[22:20]), .CLK_2(ROW4_ROW5[23]),
    .DBG_MEM({cell_61_dbg_mem_2, cell_61_dbg_mem}),
    .DBG_LED({cell_61_dbg_led[2], DBGROW4_7[0], cell_61_dbg_led[0]}));
  Hex_Digit_Display hex_digit_display_125 (.value(cell_61_dbg_mem));  // open: dp
  \cell  cell_62 (
    .SET_TAIL(cell_62_set_tail), .IS_HEAD(cell_54_set_head), .IS_ACTIVE(cell_62_is_active),
    .IS_ACTIVE_LEFT(cell_54_is_active_2), .DATA_IN(cell_54_data_in_2), .DATA_OUT_2(cell_62_data_out_2),
    .CMD(cell_54_cmd_2), .CLK(cell_54_clk_2), .IS_TAIL(ROW5_ROW6[0]), .SET_HEAD(ROW5_ROW6[1]),
    .IS_ACTIVE_RIGHT(ROW5_ROW6[2]), .IS_ACTIVE_2(ROW5_ROW6[3]), .DATA_IN_2(ROW5_ROW6[11:4]),
    .DATA_OUT(ROW5_ROW6[19:12]), .CMD_2(ROW5_ROW6[22:20]), .CLK_2(ROW5_ROW6[23]),
    .DBG_MEM({cell_62_dbg_mem_2, cell_62_dbg_mem}),
    .DBG_LED({cell_62_dbg_led[2], DBGROW4_7[8], cell_62_dbg_led[0]}));
  Hex_Digit_Display hex_digit_display_126 (.value(cell_62_dbg_mem));  // open: dp
  \cell  cell_63 (
    .SET_TAIL(cell_63_set_tail), .IS_HEAD(cell_55_set_head), .IS_ACTIVE(cell_63_is_active),
    .IS_ACTIVE_LEFT(cell_55_is_active_2), .DATA_IN(cell_55_data_in_2), .DATA_OUT_2(cell_63_data_out_2),
    .CMD(cell_55_cmd_2), .CLK(cell_55_clk_2), .IS_TAIL(ROW6_ROW7[0]), .SET_HEAD(ROW6_ROW7[1]),
    .IS_ACTIVE_RIGHT(ROW6_ROW7[2]), .IS_ACTIVE_2(ROW6_ROW7[3]), .DATA_IN_2(ROW6_ROW7[11:4]),
    .DATA_OUT(ROW6_ROW7[19:12]), .CMD_2(ROW6_ROW7[22:20]), .CLK_2(ROW6_ROW7[23]),
    .DBG_MEM({cell_63_dbg_mem_2, cell_63_dbg_mem}),
    .DBG_LED({cell_63_dbg_led[2], DBGROW4_7[16], cell_63_dbg_led[0]}));
  Hex_Digit_Display hex_digit_display_127 (.value(cell_63_dbg_mem));  // open: dp
  \cell  cell_64 (
    .SET_TAIL(cell_64_set_tail), .IS_HEAD(cell_56_set_head), .IS_ACTIVE(cell_64_is_active),
    .IS_ACTIVE_LEFT(cell_56_is_active_2), .DATA_IN(cell_56_data_in_2), .DATA_OUT_2(cell_64_data_out_2),
    .CMD(cell_56_cmd_2), .CLK(cell_56_clk_2), .IS_TAIL(IS_TAIL), .SET_HEAD(SET_HEAD),
    .IS_ACTIVE_RIGHT(IS_ACTIVE_RIGHT), .IS_ACTIVE_2(IS_ACTIVE_2), .DATA_IN_2(DATA_IN_2), .DATA_OUT(DATA_OUT),
    .CMD_2(CMD_2), .CLK_2(CLK_2), .DBG_MEM({cell_64_dbg_mem_2, cell_64_dbg_mem}),
    .DBG_LED({cell_64_dbg_led[2], DBGROW4_7[24], cell_64_dbg_led[0]}));
  Hex_Digit_Display hex_digit_display_128 (.value(cell_64_dbg_mem));  // open: dp

  // Other names for the same wires on the sheet: DBGROW0[7:0] = DBGROW0_3[7:0]; DBGROW1[7:0] = DBGROW0_3[15:8];
  //   DBGROW2[7:0] = DBGROW0_3[23:16]; DBGROW3[7:0] = DBGROW0_3[31:24]; DBGROW4[7:0] = DBGROW4_7[7:0];
  //   DBGROW5[7:0] = DBGROW4_7[15:8]; DBGROW6[7:0] = DBGROW4_7[23:16]; DBGROW7[7:0] = DBGROW4_7[31:24];
  //   ROW0LEFT[23:0] = {CLK, CMD, DATA_OUT_2, DATA_IN, IS_ACTIVE_LEFT, IS_ACTIVE, IS_HEAD, SET_TAIL};
  //   ROW7RIGHT[23:0] = {CLK_2, CMD_2, DATA_OUT, DATA_IN_2, IS_ACTIVE_2, IS_ACTIVE_RIGHT, SET_HEAD, IS_TAIL}
endmodule

module main2 (
);

  wire clock_1_out, cpu_1_cell_clk, cpu_1_fake_act, cpu_1_is_inited, cpu_1_is_on, cpu_1_kbd_clk,
       cpu_1_tape_next, cpu_1_tape_prev, cpu_1_tape_rst, cpu_1_tty_clk, cpu_1_wait_kbd, keyboard_1_avail,
       START_out;
  wire [2:0] cpu_1_cmd, undriven_3;
  wire [3:0] rom_1_data, tape_1_bf_cmd, undriven, undriven_2;
  wire [6:0] cpu_1_disp, keyboard_1_data;
  wire [7:0] cell32_1_data_out_2, cell32_1_dbgrow0_3, cell32_1_dbgrow0_3_2, cell32_1_dbgrow0_3_3,
       cell32_1_dbgrow0_3_4, cpu_1_data_to_cell;
  wire [11:0] tape_1_address;

  tape tape_1 (
    .ADDRESS(tape_1_address), .DATA(rom_1_data), .BF_CMD(tape_1_bf_cmd), .BF_NEXT(cpu_1_tape_next),
    .BF_PREV(cpu_1_tape_prev), .TAPE_RST(cpu_1_tape_rst));
  Clock clock_1 (.out(clock_1_out));
  Button START (.out(START_out));
  LED NEED_INPUT (.in(cpu_1_wait_kbd));
  Keyboard keyboard_1 (.clk(cpu_1_kbd_clk), .avail(keyboard_1_avail), .data(keyboard_1_data));  // open: re, clr
  LED IS_ON (.in(cpu_1_is_on));
  LED IS_INITED (.in(cpu_1_is_inited));
  ROM #(.addrWidth(12), .dataWidth(4)) rom_1 (.addr(tape_1_address), .data(rom_1_data));  // open: sel
  ROM #(.addrWidth(12), .dataWidth(4)) rom_2 ();  // open: addr, data, sel
  ROM #(.addrWidth(12), .dataWidth(4)) rom_3 ();  // open: addr, data, sel
  cpu cpu_1 (
    .CUR_BF(tape_1_bf_cmd), .TAPE_NEXT(cpu_1_tape_next), .TAPE_PREV(cpu_1_tape_prev),
    .TAPE_RST(cpu_1_tape_rst), .IS_INITED(cpu_1_is_inited), .IS_ON(cpu_1_is_on), .DISP(cpu_1_disp),
    .TTY_CLK(cpu_1_tty_clk), .CLK(clock_1_out), .TURN_ON(START_out), .WAIT_KBD(cpu_1_wait_kbd),
    .KBD_CLK(cpu_1_kbd_clk), .CHAR(keyboard_1_data), .HAS_CHAR(keyboard_1_avail), .FAKE_ACT(cpu_1_fake_act),
    .DATA_TO_CELL(cpu_1_data_to_cell), .DATA_FROM_CELL(cell32_1_data_out_2), .CMD(cpu_1_cmd),
    .CELL_CLK(cpu_1_cell_clk));
  TTY #(.rows(30), .cols(100)) tty_1 (.data(cpu_1_disp), .clk(cpu_1_tty_clk));  // open: we, clr
  DotMatrix #(.inputtype("row"), .matrixcols(8), .matrixrows(4)) dotmatrix_1 (
    .row0(cell32_1_dbgrow0_3), .row1(cell32_1_dbgrow0_3_2), .row2(cell32_1_dbgrow0_3_3),
    .row3(cell32_1_dbgrow0_3_4));
  cell32 cell32_1 (
    .IS_ACTIVE_LEFT(cpu_1_fake_act), .DATA_IN(cpu_1_data_to_cell), .DATA_OUT_2(cell32_1_data_out_2),
    .CMD(cpu_1_cmd), .CLK(cpu_1_cell_clk),
    .DBGROW0_3({cell32_1_dbgrow0_3_4, cell32_1_dbgrow0_3_3, cell32_1_dbgrow0_3_2, cell32_1_dbgrow0_3}));  // open: SET_TAIL, IS_HEAD, IS_ACTIVE, IS_TAIL, SET_HEAD, IS_ACTIVE_RIGHT, IS_ACTIVE_2, DATA_IN_2, DATA_OUT, CMD_2, CLK_2
  LED HAS_INPUT (.in(keyboard_1_avail));
  Hex_Digit_Display hex_digit_display_1 (.value({1'b0, keyboard_1_data[6:4]}));  // open: dp
  Hex_Digit_Display hex_digit_display_2 (.value(keyboard_1_data[3:0]));  // open: dp
  Hex_Digit_Display hex_digit_display_3 (.value(undriven_2));  // open: dp
  Hex_Digit_Display hex_digit_display_4 (.value(undriven));  // open: dp
  Hex_Digit_Display hex_digit_display_5 (.value({1'b0, undriven_3}));  // open: dp

  // Notes on the sheet:
  //   Warp digits
  //   [Hello, world]
  //   Hello, world
  //   contents of rom_1 (hex, n*v repeats v):
  //   4*3 6 3 6 6 6 3 6 6 6 5*3 6 6 6 3 3 6 1 7 5 1 10*7 1 7 7 7 1 6 2 4*6 1 3 5*7 2 7 0 6 3 1 2 6 3 8*7 1
  //   2 6 3 7 1 7 7 7 3 3 13*6 1 2 2 1 7 2 6 3 3 0 3 1 2 0 3 7 0 2 2 1 6 3 5*6 1 2 8*7 3 7 0 2 1 2 6 3 7
  //   8*0 2 1 2 2 6 6 1 11*3 6 11*2 7 0 2 2 6 3 6 3 6 3 3 3 6 3 6 3 3 6 3 6 5*2 7 1 2 2 6 3 3 3 6 3 6 3 3
  //   3 6 5*2 7 1 4*2 6 3 3 7 4*3 7 3 3 6 4*2 7 1 4*2 7 3 6 4*3 7 3 3 3 7 3 7 5*2 7 1 2 2 2 7 4*3 6 2 7 1
  //   2 2 2 6 4*3 7 3 6 3 3 6 4*2 7 1 4*2 6 3 7 3 6 3 3 3 6 4*3 6 5*2 7 1 2 2 7 3 3 3 7 3 7 3 3 3 7 5*2 7
  //   1 4*2 7 3 6 4*3 6 3 6 3 3 3 6 5*2 7 1 4*2 6 6*3 7 2 2 7 1 2 2 6 3 3 3 7 4*3 7 5*2 7 1 3 6 3 3 3 7 3
  //   6 5*2 7 1 3 3 6 2 2 7 1 2 2 2 7 3 7 3 3 3 7 3 7 3 3 6 4*2 7 1 2 2 2 6 3 6 3 3 3 6 3 6 2 2 7 1 3 7 3
  //   7 2 2 7 1 2 2 7 3 3 3 6 3 6 2 2 7 1 2 2 6 6*3 7 3 7 5*2 7 1 4*2 7 3 3 7 3 3 7 1 4*2 6 8*3 6 4*2 7 1
  //   4*2 7 3 3 6 7*3 6 5*2 7 1 3 7 3 3 3 7 4*2 7 21*0 3 1 1 11*2 6 11*3 7 0 3 0 6 7*3 6 3 3 6 2 0 3 0 2 2
  //   1 7 0 2 1 7 1 4*3 6 4*2 7 0 0 6*2 6 6 2 6 6 6 2 6 6 6 1 3 0 2 1 5*3 8*6 1 2 6*6 2 4*6 3 3 7 0 3 3 3
  //   1 7 1 2 6 4*2 4 5*3 7 0 0 2 2 6 2 2 7 4*2 1 7 1 7 1 3 6 2 7 0 3 0 3 3 3 1 4 1 3 0 0 2 2 1 2 6 3 7 0
  //   3 3 3 1 2 2 7 1 2 6 6 3 7 0 3 3 7 0 2 2 1 6 6 1 2 6 3 7 7 0 3 6 2 0 3 3 3 1 2 6 3 7 0 8*2 0 5*3 10*6
  //   4 3 6 1 1 7 0 2 0 2 2 2 0 8
  //   contents of rom_2 (hex, n*v repeats v):
  //   10*6 1 3 7*6 3 10*6 3 6 6 6 3 6 4*2 7 0 3 6 6 4 3 6 4 7*6 4 4 6 6 6 4 3 6 6 4 2 2 15*6 4 3 4 6 6 6 4
  //   6*7 4 8*7 4 3 6 4 3 4 8
  //   contents of rom_3 (hex, n*v repeats v):
  //   72*6 4 29*6 4 7*6 4 4 6 6 6 4 79*7 4 55*6 4 24*6 4 6 6 6 4 6*7 4 8*7 4 67*7 4 23*7 4 8
endmodule
// memcell32
module cell32 (
  input  IS_TAIL,
  input  IS_HEAD,
  input  IS_ACTIVE_RIGHT,
  input  IS_ACTIVE_LEFT,
  input  [7:0] DATA_IN,
  input  [7:0] DATA_OUT,
  input  [2:0] CMD,
  input  CLK,
  output SET_TAIL,
  output SET_HEAD,
  output IS_ACTIVE,
  output IS_ACTIVE_2,
  output [7:0] DATA_IN_2,
  output [7:0] DATA_OUT_2,
  output [2:0] CMD_2,
  output CLK_2,
  output [31:0] DBGROW0_3
);

  wire cell_1_clk_2, cell_1_is_active_2, cell_1_set_head, cell_2_clk_2, cell_2_is_active_2, cell_2_set_head,
       cell_3_clk_2, cell_3_is_active_2, cell_3_set_head, cell_4_clk_2, cell_4_is_active_2, cell_4_set_head,
       cell_5_clk_2, cell_5_is_active, cell_5_is_active_2, cell_5_set_head, cell_5_set_tail, cell_6_clk_2,
       cell_6_is_active, cell_6_is_active_2, cell_6_set_head, cell_6_set_tail, cell_7_clk_2,
       cell_7_is_active, cell_7_is_active_2, cell_7_set_head, cell_7_set_tail, cell_8_clk_2,
       cell_8_is_active, cell_8_is_active_2, cell_8_set_head, cell_8_set_tail, cell_9_clk_2,
       cell_9_is_active, cell_9_is_active_2, cell_9_set_head, cell_9_set_tail, cell_10_clk_2,
       cell_10_is_active, cell_10_is_active_2, cell_10_set_head, cell_10_set_tail, cell_11_clk_2,
       cell_11_is_active, cell_11_is_active_2, cell_11_set_head, cell_11_set_tail, cell_12_clk_2,
       cell_12_is_active, cell_12_is_active_2, cell_12_set_head, cell_12_set_tail, cell_13_clk_2,
       cell_13_is_active, cell_13_is_active_2, cell_13_set_head, cell_13_set_tail, cell_14_clk_2,
       cell_14_is_active, cell_14_is_active_2, cell_14_set_head, cell_14_set_tail, cell_15_clk_2,
       cell_15_is_active, cell_15_is_active_2, cell_15_set_head, cell_15_set_tail, cell_16_clk_2,
       cell_16_is_active, cell_16_is_active_2, cell_16_set_head, cell_16_set_tail, cell_17_clk_2,
       cell_17_is_active, cell_17_is_active_2, cell_17_set_head, cell_17_set_tail, cell_18_clk_2,
       cell_18_is_active, cell_18_is_active_2, cell_18_set_head, cell_18_set_tail, cell_19_clk_2,
       cell_19_is_active, cell_19_is_active_2, cell_19_set_head, cell_19_set_tail, cell_20_clk_2,
       cell_20_is_active, cell_20_is_active_2, cell_20_set_head, cell_20_set_tail, cell_21_clk_2,
       cell_21_is_active, cell_21_is_active_2, cell_21_set_head, cell_21_set_tail, cell_22_clk_2,
       cell_22_is_active, cell_22_is_active_2, cell_22_set_head, cell_22_set_tail, cell_23_clk_2,
       cell_23_is_active, cell_23_is_active_2, cell_23_set_head, cell_23_set_tail, cell_24_clk_2,
       cell_24_is_active, cell_24_is_active_2, cell_24_set_head, cell_24_set_tail, cell_25_clk_2,
       cell_25_is_active, cell_25_is_active_2, cell_25_set_head, cell_25_set_tail, cell_26_clk_2,
       cell_26_is_active, cell_26_is_active_2, cell_26_set_head, cell_26_set_tail, cell_27_clk_2,
       cell_27_is_active, cell_27_is_active_2, cell_27_set_head, cell_27_set_tail, cell_28_clk_2,
       cell_28_is_active, cell_28_is_active_2, cell_28_set_head, cell_28_set_tail, cell_29_is_active,
       cell_29_set_tail, cell_30_is_active, cell_30_set_tail, cell_31_is_active, cell_31_set_tail,
       cell_32_is_active, cell_32_set_tail;
  wire [2:0] cell_1_cmd_2, cell_1_dbg_led, cell_2_cmd_2, cell_2_dbg_led, cell_3_cmd_2, cell_3_dbg_led,
       cell_4_cmd_2, cell_4_dbg_led, cell_5_cmd_2, cell_5_dbg_led, cell_6_cmd_2, cell_6_dbg_led,
       cell_7_cmd_2, cell_7_dbg_led, cell_8_cmd_2, cell_8_dbg_led, cell_9_cmd_2, cell_9_dbg_led,
       cell_10_cmd_2, cell_10_dbg_led, cell_11_cmd_2, cell_11_dbg_led, cell_12_cmd_2, cell_12_dbg_led,
       cell_13_cmd_2, cell_13_dbg_led, cell_14_cmd_2, cell_14_dbg_led, cell_15_cmd_2, cell_15_dbg_led,
       cell_16_cmd_2, cell_16_dbg_led, cell_17_cmd_2, cell_17_dbg_led, cell_18_cmd_2, cell_18_dbg_led,
       cell_19_cmd_2, cell_19_dbg_led, cell_20_cmd_2, cell_20_dbg_led, cell_21_cmd_2, cell_21_dbg_led,
       cell_22_cmd_2, cell_22_dbg_led, cell_23_cmd_2, cell_23_dbg_led, cell_24_cmd_2, cell_24_dbg_led,
       cell_25_cmd_2, cell_25_dbg_led, cell_26_cmd_2, cell_26_dbg_led, cell_27_cmd_2, cell_27_dbg_led,
       cell_28_cmd_2, cell_28_dbg_led, cell_29_dbg_led, cell_30_dbg_led, cell_31_dbg_led, cell_32_dbg_led;
  wire [3:0] cell_1_dbg_mem, cell_1_dbg_mem_2, cell_2_dbg_mem, cell_2_dbg_mem_2, cell_4_dbg_mem,
       cell_4_dbg_mem_2, cell_6_dbg_mem, cell_6_dbg_mem_2, cell_7_dbg_mem, cell_7_dbg_mem_2, cell_8_dbg_mem,
       cell_8_dbg_mem_2, cell_9_dbg_mem, cell_9_dbg_mem_2, cell_10_dbg_mem, cell_10_dbg_mem_2,
       cell_12_dbg_mem, cell_12_dbg_mem_2, cell_13_dbg_mem, cell_13_dbg_mem_2, cell_15_dbg_mem,
       cell_15_dbg_mem_2, cell_16_dbg_mem, cell_16_dbg_mem_2, cell_17_dbg_mem, cell_17_dbg_mem_2,
       cell_18_dbg_mem, cell_18_dbg_mem_2, cell_19_dbg_mem, cell_19_dbg_mem_2, cell_21_dbg_mem,
       cell_21_dbg_mem_2, cell_23_dbg_mem, cell_23_dbg_mem_2, cell_24_dbg_mem, cell_24_dbg_mem_2,
       cell_25_dbg_mem, cell_25_dbg_mem_2, cell_26_dbg_mem, cell_26_dbg_mem_2, cell_27_dbg_mem,
       cell_27_dbg_mem_2, cell_29_dbg_mem, cell_29_dbg_mem_2, cell_30_dbg_mem, cell_30_dbg_mem_2,
       cell_31_dbg_mem, cell_31_dbg_mem_2, cell_32_dbg_mem, cell_32_dbg_mem_2;
  wire [7:0] cell_1_data_in_2, cell_2_data_in_2, cell_3_data_in_2, cell_3_dbg_mem, cell_4_data_in_2,
       cell_5_data_in_2, cell_5_data_out_2, cell_5_dbg_mem, cell_6_data_in_2, cell_6_data_out_2,
       cell_7_data_in_2, cell_7_data_out_2, cell_8_data_in_2, cell_8_data_out_2, cell_9_data_in_2,
       cell_9_data_out_2, cell_10_data_in_2, cell_10_data_out_2, cell_11_data_in_2, cell_11_data_out_2,
       cell_11_dbg_mem, cell_12_data_in_2, cell_12_data_out_2, cell_13_data_in_2, cell_13_data_out_2,
       cell_14_data_in_2, cell_14_data_out_2, cell_14_dbg_mem, cell_15_data_in_2, cell_15_data_out_2,
       cell_16_data_in_2, cell_16_data_out_2, cell_17_data_in_2, cell_17_data_out_2, cell_18_data_in_2,
       cell_18_data_out_2, cell_19_data_in_2, cell_19_data_out_2, cell_20_data_in_2, cell_20_data_out_2,
       cell_20_dbg_mem, cell_21_data_in_2, cell_21_data_out_2, cell_22_data_in_2, cell_22_data_out_2,
       cell_22_dbg_mem, cell_23_data_in_2, cell_23_data_out_2, cell_24_data_in_2, cell_24_data_out_2,
       cell_25_data_in_2, cell_25_data_out_2, cell_26_data_in_2, cell_26_data_out_2, cell_27_data_in_2,
       cell_27_data_out_2, cell_28_data_in_2, cell_28_data_out_2, cell_28_dbg_mem, cell_29_data_out_2,
       cell_30_data_out_2, cell_31_data_out_2, cell_32_data_out_2;
  wire [23:0] ROW0_ROW1, ROW1_ROW2, ROW2_ROW3;

  \cell  cell_1 (
    .SET_TAIL(SET_TAIL), .IS_HEAD(IS_HEAD), .IS_ACTIVE(IS_ACTIVE), .IS_ACTIVE_LEFT(IS_ACTIVE_LEFT),
    .DATA_IN(DATA_IN), .DATA_OUT_2(DATA_OUT_2), .CMD(CMD), .CLK(CLK), .IS_TAIL(cell_5_set_tail),
    .SET_HEAD(cell_1_set_head), .IS_ACTIVE_RIGHT(cell_5_is_active), .IS_ACTIVE_2(cell_1_is_active_2),
    .DATA_IN_2(cell_1_data_in_2), .DATA_OUT(cell_5_data_out_2), .CMD_2(cell_1_cmd_2), .CLK_2(cell_1_clk_2),
    .DBG_MEM({cell_1_dbg_mem_2, cell_1_dbg_mem}),
    .DBG_LED({cell_1_dbg_led[2], DBGROW0_3[7], cell_1_dbg_led[0]}));
  Hex_Digit_Display hex_digit_display_1 (.value(cell_1_dbg_mem));  // open: dp
  Hex_Digit_Display hex_digit_display_2 (.value(cell_1_dbg_mem_2));  // open: dp
  \cell  cell_2 (
    .SET_TAIL(ROW0_ROW1[0]), .IS_HEAD(ROW0_ROW1[1]), .IS_ACTIVE(ROW0_ROW1[2]), .IS_ACTIVE_LEFT(ROW0_ROW1[3]),
    .DATA_IN(ROW0_ROW1[11:4]), .DATA_OUT_2(ROW0_ROW1[19:12]), .CMD(ROW0_ROW1[22:20]), .CLK(ROW0_ROW1[23]),
    .IS_TAIL(cell_6_set_tail), .SET_HEAD(cell_2_set_head), .IS_ACTIVE_RIGHT(cell_6_is_active),
    .IS_ACTIVE_2(cell_2_is_active_2), .DATA_IN_2(cell_2_data_in_2), .DATA_OUT(cell_6_data_out_2),
    .CMD_2(cell_2_cmd_2), .CLK_2(cell_2_clk_2), .DBG_MEM({cell_2_dbg_mem_2, cell_2_dbg_mem}),
    .DBG_LED({cell_2_dbg_led[2], DBGROW0_3[15], cell_2_dbg_led[0]}));
  Hex_Digit_Display hex_digit_display_3 (.value(cell_2_dbg_mem));  // open: dp
  Hex_Digit_Display hex_digit_display_4 (.value(cell_2_dbg_mem_2));  // open: dp
  \cell  cell_3 (
    .SET_TAIL(ROW1_ROW2[0]), .IS_HEAD(ROW1_ROW2[1]), .IS_ACTIVE(ROW1_ROW2[2]), .IS_ACTIVE_LEFT(ROW1_ROW2[3]),
    .DATA_IN(ROW1_ROW2[11:4]), .DATA_OUT_2(ROW1_ROW2[19:12]), .CMD(ROW1_ROW2[22:20]), .CLK(ROW1_ROW2[23]),
    .IS_TAIL(cell_7_set_tail), .SET_HEAD(cell_3_set_head), .IS_ACTIVE_RIGHT(cell_7_is_active),
    .IS_ACTIVE_2(cell_3_is_active_2), .DATA_IN_2(cell_3_data_in_2), .DATA_OUT(cell_7_data_out_2),
    .CMD_2(cell_3_cmd_2), .CLK_2(cell_3_clk_2), .DBG_MEM(cell_3_dbg_mem),
    .DBG_LED({cell_3_dbg_led[2], DBGROW0_3[23], cell_3_dbg_led[0]}));
  Hex_Digit_Display hex_digit_display_5 (.value(cell_3_dbg_mem[7:4]));  // open: dp
  Hex_Digit_Display hex_digit_display_6 (.value(cell_3_dbg_mem[3:0]));  // open: dp
  \cell  cell_4 (
    .SET_TAIL(ROW2_ROW3[0]), .IS_HEAD(ROW2_ROW3[1]), .IS_ACTIVE(ROW2_ROW3[2]), .IS_ACTIVE_LEFT(ROW2_ROW3[3]),
    .DATA_IN(ROW2_ROW3[11:4]), .DATA_OUT_2(ROW2_ROW3[19:12]), .CMD(ROW2_ROW3[22:20]), .CLK(ROW2_ROW3[23]),
    .IS_TAIL(cell_8_set_tail), .SET_HEAD(cell_4_set_head), .IS_ACTIVE_RIGHT(cell_8_is_active),
    .IS_ACTIVE_2(cell_4_is_active_2), .DATA_IN_2(cell_4_data_in_2), .DATA_OUT(cell_8_data_out_2),
    .CMD_2(cell_4_cmd_2), .CLK_2(cell_4_clk_2), .DBG_MEM({cell_4_dbg_mem_2, cell_4_dbg_mem}),
    .DBG_LED({cell_4_dbg_led[2], DBGROW0_3[31], cell_4_dbg_led[0]}));
  Hex_Digit_Display hex_digit_display_7 (.value(cell_4_dbg_mem_2));  // open: dp
  Hex_Digit_Display hex_digit_display_8 (.value(cell_4_dbg_mem));  // open: dp
  \cell  cell_5 (
    .SET_TAIL(cell_5_set_tail), .IS_HEAD(cell_1_set_head), .IS_ACTIVE(cell_5_is_active),
    .IS_ACTIVE_LEFT(cell_1_is_active_2), .DATA_IN(cell_1_data_in_2), .DATA_OUT_2(cell_5_data_out_2),
    .CMD(cell_1_cmd_2), .CLK(cell_1_clk_2), .IS_TAIL(cell_9_set_tail), .SET_HEAD(cell_5_set_head),
    .IS_ACTIVE_RIGHT(cell_9_is_active), .IS_ACTIVE_2(cell_5_is_active_2), .DATA_IN_2(cell_5_data_in_2),
    .DATA_OUT(cell_9_data_out_2), .CMD_2(cell_5_cmd_2), .CLK_2(cell_5_clk_2), .DBG_MEM(cell_5_dbg_mem),
    .DBG_LED({cell_5_dbg_led[2], DBGROW0_3[6], cell_5_dbg_led[0]}));
  Hex_Digit_Display hex_digit_display_9 (.value(cell_5_dbg_mem[3:0]));  // open: dp
  Hex_Digit_Display hex_digit_display_10 (.value(cell_5_dbg_mem[7:4]));  // open: dp
  \cell  cell_6 (
    .SET_TAIL(cell_6_set_tail), .IS_HEAD(cell_2_set_head), .IS_ACTIVE(cell_6_is_active),
    .IS_ACTIVE_LEFT(cell_2_is_active_2), .DATA_IN(cell_2_data_in_2), .DATA_OUT_2(cell_6_data_out_2),
    .CMD(cell_2_cmd_2), .CLK(cell_2_clk_2), .IS_TAIL(cell_10_set_tail), .SET_HEAD(cell_6_set_head),
    .IS_ACTIVE_RIGHT(cell_10_is_active), .IS_ACTIVE_2(cell_6_is_active_2), .DATA_IN_2(cell_6_data_in_2),
    .DATA_OUT(cell_10_data_out_2), .CMD_2(cell_6_cmd_2), .CLK_2(cell_6_clk_2),
    .DBG_MEM({cell_6_dbg_mem_2, cell_6_dbg_mem}),
    .DBG_LED({cell_6_dbg_led[2], DBGROW0_3[14], cell_6_dbg_led[0]}));
  Hex_Digit_Display hex_digit_display_11 (.value(cell_6_dbg_mem));  // open: dp
  Hex_Digit_Display hex_digit_display_12 (.value(cell_6_dbg_mem_2));  // open: dp
  \cell  cell_7 (
    .SET_TAIL(cell_7_set_tail), .IS_HEAD(cell_3_set_head), .IS_ACTIVE(cell_7_is_active),
    .IS_ACTIVE_LEFT(cell_3_is_active_2), .DATA_IN(cell_3_data_in_2), .DATA_OUT_2(cell_7_data_out_2),
    .CMD(cell_3_cmd_2), .CLK(cell_3_clk_2), .IS_TAIL(cell_11_set_tail), .SET_HEAD(cell_7_set_head),
    .IS_ACTIVE_RIGHT(cell_11_is_active), .IS_ACTIVE_2(cell_7_is_active_2), .DATA_IN_2(cell_7_data_in_2),
    .DATA_OUT(cell_11_data_out_2), .CMD_2(cell_7_cmd_2), .CLK_2(cell_7_clk_2),
    .DBG_MEM({cell_7_dbg_mem_2, cell_7_dbg_mem}),
    .DBG_LED({cell_7_dbg_led[2], DBGROW0_3[22], cell_7_dbg_led[0]}));
  Hex_Digit_Display hex_digit_display_13 (.value(cell_7_dbg_mem_2));  // open: dp
  Hex_Digit_Display hex_digit_display_14 (.value(cell_7_dbg_mem));  // open: dp
  \cell  cell_8 (
    .SET_TAIL(cell_8_set_tail), .IS_HEAD(cell_4_set_head), .IS_ACTIVE(cell_8_is_active),
    .IS_ACTIVE_LEFT(cell_4_is_active_2), .DATA_IN(cell_4_data_in_2), .DATA_OUT_2(cell_8_data_out_2),
    .CMD(cell_4_cmd_2), .CLK(cell_4_clk_2), .IS_TAIL(cell_12_set_tail), .SET_HEAD(cell_8_set_head),
    .IS_ACTIVE_RIGHT(cell_12_is_active), .IS_ACTIVE_2(cell_8_is_active_2), .DATA_IN_2(cell_8_data_in_2),
    .DATA_OUT(cell_12_data_out_2), .CMD_2(cell_8_cmd_2), .CLK_2(cell_8_clk_2),
    .DBG_MEM({cell_8_dbg_mem_2, cell_8_dbg_mem}),
    .DBG_LED({cell_8_dbg_led[2], DBGROW0_3[30], cell_8_dbg_led[0]}));
  Hex_Digit_Display hex_digit_display_15 (.value(cell_8_dbg_mem_2));  // open: dp
  Hex_Digit_Display hex_digit_display_16 (.value(cell_8_dbg_mem));  // open: dp
  Hex_Digit_Display hex_digit_display_17 (.value(cell_9_dbg_mem_2));  // open: dp
  Hex_Digit_Display hex_digit_display_18 (.value(cell_10_dbg_mem_2));  // open: dp
  Hex_Digit_Display hex_digit_display_19 (.value(cell_11_dbg_mem[7:4]));  // open: dp
  Hex_Digit_Display hex_digit_display_20 (.value(cell_12_dbg_mem_2));  // open: dp
  \cell  cell_9 (
    .SET_TAIL(cell_9_set_tail), .IS_HEAD(cell_5_set_head), .IS_ACTIVE(cell_9_is_active),
    .IS_ACTIVE_LEFT(cell_5_is_active_2), .DATA_IN(cell_5_data_in_2), .DATA_OUT_2(cell_9_data_out_2),
    .CMD(cell_5_cmd_2), .CLK(cell_5_clk_2), .IS_TAIL(cell_13_set_tail), .SET_HEAD(cell_9_set_head),
    .IS_ACTIVE_RIGHT(cell_13_is_active), .IS_ACTIVE_2(cell_9_is_active_2), .DATA_IN_2(cell_9_data_in_2),
    .DATA_OUT(cell_13_data_out_2), .CMD_2(cell_9_cmd_2), .CLK_2(cell_9_clk_2),
    .DBG_MEM({cell_9_dbg_mem_2, cell_9_dbg_mem}),
    .DBG_LED({cell_9_dbg_led[2], DBGROW0_3[5], cell_9_dbg_led[0]}));
  Hex_Digit_Display hex_digit_display_21 (.value(cell_9_dbg_mem));  // open: dp
  \cell  cell_10 (
    .SET_TAIL(cell_10_set_tail), .IS_HEAD(cell_6_set_head), .IS_ACTIVE(cell_10_is_active),
    .IS_ACTIVE_LEFT(cell_6_is_active_2), .DATA_IN(cell_6_data_in_2), .DATA_OUT_2(cell_10_data_out_2),
    .CMD(cell_6_cmd_2), .CLK(cell_6_clk_2), .IS_TAIL(cell_14_set_tail), .SET_HEAD(cell_10_set_head),
    .IS_ACTIVE_RIGHT(cell_14_is_active), .IS_ACTIVE_2(cell_10_is_active_2), .DATA_IN_2(cell_10_data_in_2),
    .DATA_OUT(cell_14_data_out_2), .CMD_2(cell_10_cmd_2), .CLK_2(cell_10_clk_2),
    .DBG_MEM({cell_10_dbg_mem_2, cell_10_dbg_mem}),
    .DBG_LED({cell_10_dbg_led[2], DBGROW0_3[13], cell_10_dbg_led[0]}));
  Hex_Digit_Display hex_digit_display_22 (.value(cell_10_dbg_mem));  // open: dp
  \cell  cell_11 (
    .SET_TAIL(cell_11_set_tail), .IS_HEAD(cell_7_set_head), .IS_ACTIVE(cell_11_is_active),
    .IS_ACTIVE_LEFT(cell_7_is_active_2), .DATA_IN(cell_7_data_in_2), .DATA_OUT_2(cell_11_data_out_2),
    .CMD(cell_7_cmd_2), .CLK(cell_7_clk_2), .IS_TAIL(cell_15_set_tail), .SET_HEAD(cell_11_set_head),
    .IS_ACTIVE_RIGHT(cell_15_is_active), .IS_ACTIVE_2(cell_11_is_active_2), .DATA_IN_2(cell_11_data_in_2),
    .DATA_OUT(cell_15_data_out_2), .CMD_2(cell_11_cmd_2), .CLK_2(cell_11_clk_2), .DBG_MEM(cell_11_dbg_mem),
    .DBG_LED({cell_11_dbg_led[2], DBGROW0_3[21], cell_11_dbg_led[0]}));
  Hex_Digit_Display hex_digit_display_23 (.value(cell_11_dbg_mem[3:0]));  // open: dp
  \cell  cell_12 (
    .SET_TAIL(cell_12_set_tail), .IS_HEAD(cell_8_set_head), .IS_ACTIVE(cell_12_is_active),
    .IS_ACTIVE_LEFT(cell_8_is_active_2), .DATA_IN(cell_8_data_in_2), .DATA_OUT_2(cell_12_data_out_2),
    .CMD(cell_8_cmd_2), .CLK(cell_8_clk_2), .IS_TAIL(cell_16_set_tail), .SET_HEAD(cell_12_set_head),
    .IS_ACTIVE_RIGHT(cell_16_is_active), .IS_ACTIVE_2(cell_12_is_active_2), .DATA_IN_2(cell_12_data_in_2),
    .DATA_OUT(cell_16_data_out_2), .CMD_2(cell_12_cmd_2), .CLK_2(cell_12_clk_2),
    .DBG_MEM({cell_12_dbg_mem_2, cell_12_dbg_mem}),
    .DBG_LED({cell_12_dbg_led[2], DBGROW0_3[29], cell_12_dbg_led[0]}));
  Hex_Digit_Display hex_digit_display_24 (.value(cell_12_dbg_mem));  // open: dp
  \cell  cell_13 (
    .SET_TAIL(cell_13_set_tail), .IS_HEAD(cell_9_set_head), .IS_ACTIVE(cell_13_is_active),
    .IS_ACTIVE_LEFT(cell_9_is_active_2), .DATA_IN(cell_9_data_in_2), .DATA_OUT_2(cell_13_data_out_2),
    .CMD(cell_9_cmd_2), .CLK(cell_9_clk_2), .IS_TAIL(cell_17_set_tail), .SET_HEAD(cell_13_set_head),
    .IS_ACTIVE_RIGHT(cell_17_is_active), .IS_ACTIVE_2(cell_13_is_active_2), .DATA_IN_2(cell_13_data_in_2),
    .DATA_OUT(cell_17_data_out_2), .CMD_2(cell_13_cmd_2), .CLK_2(cell_13_clk_2),
    .DBG_MEM({cell_13_dbg_mem_2, cell_13_dbg_mem}),
    .DBG_LED({cell_13_dbg_led[2], DBGROW0_3[4], cell_13_dbg_led[0]}));
  Hex_Digit_Display hex_digit_display_25 (.value(cell_13_dbg_mem));  // open: dp
  Hex_Digit_Display hex_digit_display_26 (.value(cell_13_dbg_mem_2));  // open: dp
  \cell  cell_14 (
    .SET_TAIL(cell_14_set_tail), .IS_HEAD(cell_10_set_head), .IS_ACTIVE(cell_14_is_active),
    .IS_ACTIVE_LEFT(cell_10_is_active_2), .DATA_IN(cell_10_data_in_2), .DATA_OUT_2(cell_14_data_out_2),
    .CMD(cell_10_cmd_2), .CLK(cell_10_clk_2), .IS_TAIL(cell_18_set_tail), .SET_HEAD(cell_14_set_head),
    .IS_ACTIVE_RIGHT(cell_18_is_active), .IS_ACTIVE_2(cell_14_is_active_2), .DATA_IN_2(cell_14_data_in_2),
    .DATA_OUT(cell_18_data_out_2), .CMD_2(cell_14_cmd_2), .CLK_2(cell_14_clk_2), .DBG_MEM(cell_14_dbg_mem),
    .DBG_LED({cell_14_dbg_led[2], DBGROW0_3[12], cell_14_dbg_led[0]}));
  Hex_Digit_Display hex_digit_display_27 (.value(cell_14_dbg_mem[3:0]));  // open: dp
  Hex_Digit_Display hex_digit_display_28 (.value(cell_14_dbg_mem[7:4]));  // open: dp
  \cell  cell_15 (
    .SET_TAIL(cell_15_set_tail), .IS_HEAD(cell_11_set_head), .IS_ACTIVE(cell_15_is_active),
    .IS_ACTIVE_LEFT(cell_11_is_active_2), .DATA_IN(cell_11_data_in_2), .DATA_OUT_2(cell_15_data_out_2),
    .CMD(cell_11_cmd_2), .CLK(cell_11_clk_2), .IS_TAIL(cell_19_set_tail), .SET_HEAD(cell_15_set_head),
    .IS_ACTIVE_RIGHT(cell_19_is_active), .IS_ACTIVE_2(cell_15_is_active_2), .DATA_IN_2(cell_15_data_in_2),
    .DATA_OUT(cell_19_data_out_2), .CMD_2(cell_15_cmd_2), .CLK_2(cell_15_clk_2),
    .DBG_MEM({cell_15_dbg_mem_2, cell_15_dbg_mem}),
    .DBG_LED({cell_15_dbg_led[2], DBGROW0_3[20], cell_15_dbg_led[0]}));
  Hex_Digit_Display hex_digit_display_29 (.value(cell_15_dbg_mem_2));  // open: dp
  Hex_Digit_Display hex_digit_display_30 (.value(cell_15_dbg_mem));  // open: dp
  \cell  cell_16 (
    .SET_TAIL(cell_16_set_tail), .IS_HEAD(cell_12_set_head), .IS_ACTIVE(cell_16_is_active),
    .IS_ACTIVE_LEFT(cell_12_is_active_2), .DATA_IN(cell_12_data_in_2), .DATA_OUT_2(cell_16_data_out_2),
    .CMD(cell_12_cmd_2), .CLK(cell_12_clk_2), .IS_TAIL(cell_20_set_tail), .SET_HEAD(cell_16_set_head),
    .IS_ACTIVE_RIGHT(cell_20_is_active), .IS_ACTIVE_2(cell_16_is_active_2), .DATA_IN_2(cell_16_data_in_2),
    .DATA_OUT(cell_20_data_out_2), .CMD_2(cell_16_cmd_2), .CLK_2(cell_16_clk_2),
    .DBG_MEM({cell_16_dbg_mem_2, cell_16_dbg_mem}),
    .DBG_LED({cell_16_dbg_led[2], DBGROW0_3[28], cell_16_dbg_led[0]}));
  Hex_Digit_Display hex_digit_display_31 (.value(cell_16_dbg_mem_2));  // open: dp
  Hex_Digit_Display hex_digit_display_32 (.value(cell_16_dbg_mem));  // open: dp
  \cell  cell_17 (
    .SET_TAIL(cell_17_set_tail), .IS_HEAD(cell_13_set_head), .IS_ACTIVE(cell_17_is_active),
    .IS_ACTIVE_LEFT(cell_13_is_active_2), .DATA_IN(cell_13_data_in_2), .DATA_OUT_2(cell_17_data_out_2),
    .CMD(cell_13_cmd_2), .CLK(cell_13_clk_2), .IS_TAIL(cell_21_set_tail), .SET_HEAD(cell_17_set_head),
    .IS_ACTIVE_RIGHT(cell_21_is_active), .IS_ACTIVE_2(cell_17_is_active_2), .DATA_IN_2(cell_17_data_in_2),
    .DATA_OUT(cell_21_data_out_2), .CMD_2(cell_17_cmd_2), .CLK_2(cell_17_clk_2),
    .DBG_MEM({cell_17_dbg_mem_2, cell_17_dbg_mem}),
    .DBG_LED({cell_17_dbg_led[2], DBGROW0_3[3], cell_17_dbg_led[0]}));
  Hex_Digit_Display hex_digit_display_33 (.value(cell_17_dbg_mem_2));  // open: dp
  \cell  cell_18 (
    .SET_TAIL(cell_18_set_tail), .IS_HEAD(cell_14_set_head), .IS_ACTIVE(cell_18_is_active),
    .IS_ACTIVE_LEFT(cell_14_is_active_2), .DATA_IN(cell_14_data_in_2), .DATA_OUT_2(cell_18_data_out_2),
    .CMD(cell_14_cmd_2), .CLK(cell_14_clk_2), .IS_TAIL(cell_22_set_tail), .SET_HEAD(cell_18_set_head),
    .IS_ACTIVE_RIGHT(cell_22_is_active), .IS_ACTIVE_2(cell_18_is_active_2), .DATA_IN_2(cell_18_data_in_2),
    .DATA_OUT(cell_22_data_out_2), .CMD_2(cell_18_cmd_2), .CLK_2(cell_18_clk_2),
    .DBG_MEM({cell_18_dbg_mem_2, cell_18_dbg_mem}),
    .DBG_LED({cell_18_dbg_led[2], DBGROW0_3[11], cell_18_dbg_led[0]}));
  Hex_Digit_Display hex_digit_display_34 (.value(cell_18_dbg_mem_2));  // open: dp
  \cell  cell_19 (
    .SET_TAIL(cell_19_set_tail), .IS_HEAD(cell_15_set_head), .IS_ACTIVE(cell_19_is_active),
    .IS_ACTIVE_LEFT(cell_15_is_active_2), .DATA_IN(cell_15_data_in_2), .DATA_OUT_2(cell_19_data_out_2),
    .CMD(cell_15_cmd_2), .CLK(cell_15_clk_2), .IS_TAIL(cell_23_set_tail), .SET_HEAD(cell_19_set_head),
    .IS_ACTIVE_RIGHT(cell_23_is_active), .IS_ACTIVE_2(cell_19_is_active_2), .DATA_IN_2(cell_19_data_in_2),
    .DATA_OUT(cell_23_data_out_2), .CMD_2(cell_19_cmd_2), .CLK_2(cell_19_clk_2),
    .DBG_MEM({cell_19_dbg_mem_2, cell_19_dbg_mem}),
    .DBG_LED({cell_19_dbg_led[2], DBGROW0_3[19], cell_19_dbg_led[0]}));
  Hex_Digit_Display hex_digit_display_35 (.value(cell_19_dbg_mem_2));  // open: dp
  \cell  cell_20 (
    .SET_TAIL(cell_20_set_tail), .IS_HEAD(cell_16_set_head), .IS_ACTIVE(cell_20_is_active),
    .IS_ACTIVE_LEFT(cell_16_is_active_2), .DATA_IN(cell_16_data_in_2), .DATA_OUT_2(cell_20_data_out_2),
    .CMD(cell_16_cmd_2), .CLK(cell_16_clk_2), .IS_TAIL(cell_24_set_tail), .SET_HEAD(cell_20_set_head),
    .IS_ACTIVE_RIGHT(cell_24_is_active), .IS_ACTIVE_2(cell_20_is_active_2), .DATA_IN_2(cell_20_data_in_2),
    .DATA_OUT(cell_24_data_out_2), .CMD_2(cell_20_cmd_2), .CLK_2(cell_20_clk_2), .DBG_MEM(cell_20_dbg_mem),
    .DBG_LED({cell_20_dbg_led[2], DBGROW0_3[27], cell_20_dbg_led[0]}));
  Hex_Digit_Display hex_digit_display_36 (.value(cell_20_dbg_mem[7:4]));  // open: dp
  Hex_Digit_Display hex_digit_display_37 (.value(cell_17_dbg_mem));  // open: dp
  Hex_Digit_Display hex_digit_display_38 (.value(cell_21_dbg_mem_2));  // open: dp
  Hex_Digit_Display hex_digit_display_39 (.value(cell_18_dbg_mem));  // open: dp
  Hex_Digit_Display hex_digit_display_40 (.value(cell_22_dbg_mem[7:4]));  // open: dp
  Hex_Digit_Display hex_digit_display_41 (.value(cell_19_dbg_mem));  // open: dp
  Hex_Digit_Display hex_digit_display_42 (.value(cell_23_dbg_mem_2));  // open: dp
  Hex_Digit_Display hex_digit_display_43 (.value(cell_24_dbg_mem_2));  // open: dp
  Hex_Digit_Display hex_digit_display_44 (.value(cell_20_dbg_mem[3:0]));  // open: dp
  \cell  cell_21 (
    .SET_TAIL(cell_21_set_tail), .IS_HEAD(cell_17_set_head), .IS_ACTIVE(cell_21_is_active),
    .IS_ACTIVE_LEFT(cell_17_is_active_2), .DATA_IN(cell_17_data_in_2), .DATA_OUT_2(cell_21_data_out_2),
    .CMD(cell_17_cmd_2), .CLK(cell_17_clk_2), .IS_TAIL(cell_25_set_tail), .SET_HEAD(cell_21_set_head),
    .IS_ACTIVE_RIGHT(cell_25_is_active), .IS_ACTIVE_2(cell_21_is_active_2), .DATA_IN_2(cell_21_data_in_2),
    .DATA_OUT(cell_25_data_out_2), .CMD_2(cell_21_cmd_2), .CLK_2(cell_21_clk_2),
    .DBG_MEM({cell_21_dbg_mem_2, cell_21_dbg_mem}),
    .DBG_LED({cell_21_dbg_led[2], DBGROW0_3[2], cell_21_dbg_led[0]}));
  Hex_Digit_Display hex_digit_display_45 (.value(cell_21_dbg_mem));  // open: dp
  \cell  cell_22 (
    .SET_TAIL(cell_22_set_tail), .IS_HEAD(cell_18_set_head), .IS_ACTIVE(cell_22_is_active),
    .IS_ACTIVE_LEFT(cell_18_is_active_2), .DATA_IN(cell_18_data_in_2), .DATA_OUT_2(cell_22_data_out_2),
    .CMD(cell_18_cmd_2), .CLK(cell_18_clk_2), .IS_TAIL(cell_26_set_tail), .SET_HEAD(cell_22_set_head),
    .IS_ACTIVE_RIGHT(cell_26_is_active), .IS_ACTIVE_2(cell_22_is_active_2), .DATA_IN_2(cell_22_data_in_2),
    .DATA_OUT(cell_26_data_out_2), .CMD_2(cell_22_cmd_2), .CLK_2(cell_22_clk_2), .DBG_MEM(cell_22_dbg_mem),
    .DBG_LED({cell_22_dbg_led[2], DBGROW0_3[10], cell_22_dbg_led[0]}));
  Hex_Digit_Display hex_digit_display_46 (.value(cell_22_dbg_mem[3:0]));  // open: dp
  \cell  cell_23 (
    .SET_TAIL(cell_23_set_tail), .IS_HEAD(cell_19_set_head), .IS_ACTIVE(cell_23_is_active),
    .IS_ACTIVE_LEFT(cell_19_is_active_2), .DATA_IN(cell_19_data_in_2), .DATA_OUT_2(cell_23_data_out_2),
    .CMD(cell_19_cmd_2), .CLK(cell_19_clk_2), .IS_TAIL(cell_27_set_tail), .SET_HEAD(cell_23_set_head),
    .IS_ACTIVE_RIGHT(cell_27_is_active), .IS_ACTIVE_2(cell_23_is_active_2), .DATA_IN_2(cell_23_data_in_2),
    .DATA_OUT(cell_27_data_out_2), .CMD_2(cell_23_cmd_2), .CLK_2(cell_23_clk_2),
    .DBG_MEM({cell_23_dbg_mem_2, cell_23_dbg_mem}),
    .DBG_LED({cell_23_dbg_led[2], DBGROW0_3[18], cell_23_dbg_led[0]}));
  Hex_Digit_Display hex_digit_display_47 (.value(cell_23_dbg_mem));  // open: dp
  \cell  cell_24 (
    .SET_TAIL(cell_24_set_tail), .IS_HEAD(cell_20_set_head), .IS_ACTIVE(cell_24_is_active),
    .IS_ACTIVE_LEFT(cell_20_is_active_2), .DATA_IN(cell_20_data_in_2), .DATA_OUT_2(cell_24_data_out_2),
    .CMD(cell_20_cmd_2), .CLK(cell_20_clk_2), .IS_TAIL(cell_28_set_tail), .SET_HEAD(cell_24_set_head),
    .IS_ACTIVE_RIGHT(cell_28_is_active), .IS_ACTIVE_2(cell_24_is_active_2), .DATA_IN_2(cell_24_data_in_2),
    .DATA_OUT(cell_28_data_out_2), .CMD_2(cell_24_cmd_2), .CLK_2(cell_24_clk_2),
    .DBG_MEM({cell_24_dbg_mem_2, cell_24_dbg_mem}),
    .DBG_LED({cell_24_dbg_led[2], DBGROW0_3[26], cell_24_dbg_led[0]}));
  Hex_Digit_Display hex_digit_display_48 (.value(cell_24_dbg_mem));  // open: dp
  \cell  cell_25 (
    .SET_TAIL(cell_25_set_tail), .IS_HEAD(cell_21_set_head), .IS_ACTIVE(cell_25_is_active),
    .IS_ACTIVE_LEFT(cell_21_is_active_2), .DATA_IN(cell_21_data_in_2), .DATA_OUT_2(cell_25_data_out_2),
    .CMD(cell_21_cmd_2), .CLK(cell_21_clk_2), .IS_TAIL(cell_29_set_tail), .SET_HEAD(cell_25_set_head),
    .IS_ACTIVE_RIGHT(cell_29_is_active), .IS_ACTIVE_2(cell_25_is_active_2), .DATA_IN_2(cell_25_data_in_2),
    .DATA_OUT(cell_29_data_out_2), .CMD_2(cell_25_cmd_2), .CLK_2(cell_25_clk_2),
    .DBG_MEM({cell_25_dbg_mem_2, cell_25_dbg_mem}),
    .DBG_LED({cell_25_dbg_led[2], DBGROW0_3[1], cell_25_dbg_led[0]}));
  Hex_Digit_Display hex_digit_display_49 (.value(cell_25_dbg_mem));  // open: dp
  Hex_Digit_Display hex_digit_display_50 (.value(cell_25_dbg_mem_2));  // open: dp
  \cell  cell_26 (
    .SET_TAIL(cell_26_set_tail), .IS_HEAD(cell_22_set_head), .IS_ACTIVE(cell_26_is_active),
    .IS_ACTIVE_LEFT(cell_22_is_active_2), .DATA_IN(cell_22_data_in_2), .DATA_OUT_2(cell_26_data_out_2),
    .CMD(cell_22_cmd_2), .CLK(cell_22_clk_2), .IS_TAIL(cell_30_set_tail), .SET_HEAD(cell_26_set_head),
    .IS_ACTIVE_RIGHT(cell_30_is_active), .IS_ACTIVE_2(cell_26_is_active_2), .DATA_IN_2(cell_26_data_in_2),
    .DATA_OUT(cell_30_data_out_2), .CMD_2(cell_26_cmd_2), .CLK_2(cell_26_clk_2),
    .DBG_MEM({cell_26_dbg_mem_2, cell_26_dbg_mem}),
    .DBG_LED({cell_26_dbg_led[2], DBGROW0_3[9], cell_26_dbg_led[0]}));
  Hex_Digit_Display hex_digit_display_51 (.value(cell_26_dbg_mem_2));  // open: dp
  Hex_Digit_Display hex_digit_display_52 (.value(cell_26_dbg_mem));  // open: dp
  \cell  cell_27 (
    .SET_TAIL(cell_27_set_tail), .IS_HEAD(cell_23_set_head), .IS_ACTIVE(cell_27_is_active),
    .IS_ACTIVE_LEFT(cell_23_is_active_2), .DATA_IN(cell_23_data_in_2), .DATA_OUT_2(cell_27_data_out_2),
    .CMD(cell_23_cmd_2), .CLK(cell_23_clk_2), .IS_TAIL(cell_31_set_tail), .SET_HEAD(cell_27_set_head),
    .IS_ACTIVE_RIGHT(cell_31_is_active), .IS_ACTIVE_2(cell_27_is_active_2), .DATA_IN_2(cell_27_data_in_2),
    .DATA_OUT(cell_31_data_out_2), .CMD_2(cell_27_cmd_2), .CLK_2(cell_27_clk_2),
    .DBG_MEM({cell_27_dbg_mem_2, cell_27_dbg_mem}),
    .DBG_LED({cell_27_dbg_led[2], DBGROW0_3[17], cell_27_dbg_led[0]}));
  Hex_Digit_Display hex_digit_display_53 (.value(cell_27_dbg_mem));  // open: dp
  Hex_Digit_Display hex_digit_display_54 (.value(cell_27_dbg_mem_2));  // open: dp
  \cell  cell_28 (
    .SET_TAIL(cell_28_set_tail), .IS_HEAD(cell_24_set_head), .IS_ACTIVE(cell_28_is_active),
    .IS_ACTIVE_LEFT(cell_24_is_active_2), .DATA_IN(cell_24_data_in_2), .DATA_OUT_2(cell_28_data_out_2),
    .CMD(cell_24_cmd_2), .CLK(cell_24_clk_2), .IS_TAIL(cell_32_set_tail), .SET_HEAD(cell_28_set_head),
    .IS_ACTIVE_RIGHT(cell_32_is_active), .IS_ACTIVE_2(cell_28_is_active_2), .DATA_IN_2(cell_28_data_in_2),
    .DATA_OUT(cell_32_data_out_2), .CMD_2(cell_28_cmd_2), .CLK_2(cell_28_clk_2), .DBG_MEM(cell_28_dbg_mem),
    .DBG_LED({cell_28_dbg_led[2], DBGROW0_3[25], cell_28_dbg_led[0]}));
  Hex_Digit_Display hex_digit_display_55 (.value(cell_28_dbg_mem[3:0]));  // open: dp
  Hex_Digit_Display hex_digit_display_56 (.value(cell_28_dbg_mem[7:4]));  // open: dp
  Hex_Digit_Display hex_digit_display_57 (.value(cell_29_dbg_mem_2));  // open: dp
  Hex_Digit_Display hex_digit_display_58 (.value(cell_30_dbg_mem_2));  // open: dp
  Hex_Digit_Display hex_digit_display_59 (.value(cell_31_dbg_mem_2));  // open: dp
  Hex_Digit_Display hex_digit_display_60 (.value(cell_32_dbg_mem_2));  // open: dp
  \cell  cell_29 (
    .SET_TAIL(cell_29_set_tail), .IS_HEAD(cell_25_set_head), .IS_ACTIVE(cell_29_is_active),
    .IS_ACTIVE_LEFT(cell_25_is_active_2), .DATA_IN(cell_25_data_in_2), .DATA_OUT_2(cell_29_data_out_2),
    .CMD(cell_25_cmd_2), .CLK(cell_25_clk_2), .IS_TAIL(ROW0_ROW1[0]), .SET_HEAD(ROW0_ROW1[1]),
    .IS_ACTIVE_RIGHT(ROW0_ROW1[2]), .IS_ACTIVE_2(ROW0_ROW1[3]), .DATA_IN_2(ROW0_ROW1[11:4]),
    .DATA_OUT(ROW0_ROW1[19:12]), .CMD_2(ROW0_ROW1[22:20]), .CLK_2(ROW0_ROW1[23]),
    .DBG_MEM({cell_29_dbg_mem_2, cell_29_dbg_mem}),
    .DBG_LED({cell_29_dbg_led[2], DBGROW0_3[0], cell_29_dbg_led[0]}));
  Hex_Digit_Display hex_digit_display_61 (.value(cell_29_dbg_mem));  // open: dp
  \cell  cell_30 (
    .SET_TAIL(cell_30_set_tail), .IS_HEAD(cell_26_set_head), .IS_ACTIVE(cell_30_is_active),
    .IS_ACTIVE_LEFT(cell_26_is_active_2), .DATA_IN(cell_26_data_in_2), .DATA_OUT_2(cell_30_data_out_2),
    .CMD(cell_26_cmd_2), .CLK(cell_26_clk_2), .IS_TAIL(ROW1_ROW2[0]), .SET_HEAD(ROW1_ROW2[1]),
    .IS_ACTIVE_RIGHT(ROW1_ROW2[2]), .IS_ACTIVE_2(ROW1_ROW2[3]), .DATA_IN_2(ROW1_ROW2[11:4]),
    .DATA_OUT(ROW1_ROW2[19:12]), .CMD_2(ROW1_ROW2[22:20]), .CLK_2(ROW1_ROW2[23]),
    .DBG_MEM({cell_30_dbg_mem_2, cell_30_dbg_mem}),
    .DBG_LED({cell_30_dbg_led[2], DBGROW0_3[8], cell_30_dbg_led[0]}));
  Hex_Digit_Display hex_digit_display_62 (.value(cell_30_dbg_mem));  // open: dp
  \cell  cell_31 (
    .SET_TAIL(cell_31_set_tail), .IS_HEAD(cell_27_set_head), .IS_ACTIVE(cell_31_is_active),
    .IS_ACTIVE_LEFT(cell_27_is_active_2), .DATA_IN(cell_27_data_in_2), .DATA_OUT_2(cell_31_data_out_2),
    .CMD(cell_27_cmd_2), .CLK(cell_27_clk_2), .IS_TAIL(ROW2_ROW3[0]), .SET_HEAD(ROW2_ROW3[1]),
    .IS_ACTIVE_RIGHT(ROW2_ROW3[2]), .IS_ACTIVE_2(ROW2_ROW3[3]), .DATA_IN_2(ROW2_ROW3[11:4]),
    .DATA_OUT(ROW2_ROW3[19:12]), .CMD_2(ROW2_ROW3[22:20]), .CLK_2(ROW2_ROW3[23]),
    .DBG_MEM({cell_31_dbg_mem_2, cell_31_dbg_mem}),
    .DBG_LED({cell_31_dbg_led[2], DBGROW0_3[16], cell_31_dbg_led[0]}));
  Hex_Digit_Display hex_digit_display_63 (.value(cell_31_dbg_mem));  // open: dp
  \cell  cell_32 (
    .SET_TAIL(cell_32_set_tail), .IS_HEAD(cell_28_set_head), .IS_ACTIVE(cell_32_is_active),
    .IS_ACTIVE_LEFT(cell_28_is_active_2), .DATA_IN(cell_28_data_in_2), .DATA_OUT_2(cell_32_data_out_2),
    .CMD(cell_28_cmd_2), .CLK(cell_28_clk_2), .IS_TAIL(IS_TAIL), .SET_HEAD(SET_HEAD),
    .IS_ACTIVE_RIGHT(IS_ACTIVE_RIGHT), .IS_ACTIVE_2(IS_ACTIVE_2), .DATA_IN_2(DATA_IN_2), .DATA_OUT(DATA_OUT),
    .CMD_2(CMD_2), .CLK_2(CLK_2), .DBG_MEM({cell_32_dbg_mem_2, cell_32_dbg_mem}),
    .DBG_LED({cell_32_dbg_led[2], DBGROW0_3[24], cell_32_dbg_led[0]}));
  Hex_Digit_Display hex_digit_display_64 (.value(cell_32_dbg_mem));  // open: dp

  // Other names for the same wires on the sheet: DBGROW0[7:0] = DBGROW0_3[7:0]; DBGROW1[7:0] = DBGROW0_3[15:8];
  //   DBGROW2[7:0] = DBGROW0_3[23:16]; DBGROW3[7:0] = DBGROW0_3[31:24];
  //   ROW0LEFT[23:0] = {CLK, CMD, DATA_OUT_2, DATA_IN, IS_ACTIVE_LEFT, IS_ACTIVE, IS_HEAD, SET_TAIL};
  //   ROW3RIGHT[23:0] = {CLK_2, CMD_2, DATA_OUT, DATA_IN_2, IS_ACTIVE_2, IS_ACTIVE_RIGHT, SET_HEAD, IS_TAIL}
endmodule
